// Logisim project BancoReg_j9YFN9e.circ as structural Verilog: 5 circuits, main circuit main
module main (
  input  in_1,
  input  [2:0] in_2,
  input  [1:0] in_3,
  input  [2:0] in_4,
  input  [2:0] in_5,
  input  in_6,
  input  [3:0] in_7
);

  wire [3:0] br_1_datax, br_1_datay, multiplexer_1_out, ula_1_ula__result;

  BR br_1 (
    .DataRegX(in_4), .WR(in_1), .regWR(in_2), .DataRegY(in_5), .DataIN(ula_1_ula__result),
    .DataX(br_1_datax), .DataY(br_1_datay));
  Hex_Digit_Display hex_digit_display_1 (.value(br_1_datax));  // open: dp
  Hex_Digit_Display hex_digit_display_2 (.value(br_1_datay));  // open: dp
  Multiplexer #(.width(4), .enable("false")) multiplexer_1 (
    .in0(br_1_datay), .in1(in_7), .out(multiplexer_1_out), .sel(in_6));
  ULA ula_1 (.A(br_1_datax), .B(multiplexer_1_out), .OpCode(in_3), .ULA__Result(ula_1_ula__result));
endmodule

module reg4bits (
  input  [3:0] DataIN,
  input  WR,
  output [3:0] RegDATA,
  output [3:0] DataINRelay
);

  D_Flip_Flop d_ff_1 (.clk(WR), .D(DataIN[3]), .Q(RegDATA[3]));  // open: Qn, preset, en, reset
  D_Flip_Flop d_ff_2 (.clk(WR), .D(DataIN[2]), .Q(RegDATA[2]));  // open: Qn, preset, en, reset
  D_Flip_Flop d_ff_3 (.clk(WR), .D(DataIN[1]), .Q(RegDATA[1]));  // open: Qn, preset, en, reset
  D_Flip_Flop d_ff_4 (.clk(WR), .D(DataIN[0]), .Q(RegDATA[0]));  // open: Qn, preset, en, reset

  assign DataINRelay = DataIN;
endmodule

module BR (
  input  [3:0] DataIN,
  input  [2:0] DataRegX,
  input  WR,
  input  [2:0] regWR,
  input  [2:0] DataRegY,
  output [3:0] DataX,
  output [3:0] DataY
);

  wire demultiplexer_1_out1, demultiplexer_1_out2, demultiplexer_1_out3, demultiplexer_1_out4,
       demultiplexer_1_out5, demultiplexer_1_out6, demultiplexer_1_out7;
  wire [3:0] reg4bits_1_datainrelay, reg4bits_1_regdata, reg4bits_2_datainrelay, reg4bits_2_regdata,
       reg4bits_3_datainrelay, reg4bits_3_regdata, reg4bits_4_datainrelay, reg4bits_4_regdata,
       reg4bits_5_datainrelay, reg4bits_5_regdata, reg4bits_6_datainrelay, reg4bits_6_regdata,
       reg4bits_7_regdata;

  Demultiplexer #(.select(3), .enable("false")) demultiplexer_1 (
    .out1(demultiplexer_1_out1), .out2(demultiplexer_1_out2), .out3(demultiplexer_1_out3),
    .out4(demultiplexer_1_out4), .out5(demultiplexer_1_out5), .out6(demultiplexer_1_out6),
    .out7(demultiplexer_1_out7), .in(WR), .sel(regWR));  // open: out0
  Hex_Digit_Display hex_digit_display_1 (.value(DataIN));  // open: dp
  reg4bits reg4bits_1 (
    .WR(demultiplexer_1_out1), .DataIN(DataIN), .DataINRelay(reg4bits_1_datainrelay),
    .RegDATA(reg4bits_1_regdata));
  reg4bits reg4bits_2 (
    .WR(demultiplexer_1_out2), .DataIN(reg4bits_1_datainrelay), .DataINRelay(reg4bits_2_datainrelay),
    .RegDATA(reg4bits_2_regdata));
  reg4bits reg4bits_3 (
    .WR(demultiplexer_1_out3), .DataIN(reg4bits_2_datainrelay), .DataINRelay(reg4bits_3_datainrelay),
    .RegDATA(reg4bits_3_regdata));
  reg4bits reg4bits_4 (
    .WR(demultiplexer_1_out4), .DataIN(reg4bits_3_datainrelay), .DataINRelay(reg4bits_4_datainrelay),
    .RegDATA(reg4bits_4_regdata));
  reg4bits reg4bits_5 (
    .WR(demultiplexer_1_out5), .DataIN(reg4bits_4_datainrelay), .DataINRelay(reg4bits_5_datainrelay),
    .RegDATA(reg4bits_5_regdata));
  reg4bits reg4bits_6 (
    .WR(demultiplexer_1_out6), .DataIN(reg4bits_5_datainrelay), .DataINRelay(reg4bits_6_datainrelay),
    .RegDATA(reg4bits_6_regdata));
  reg4bits reg4bits_7 (
    .WR(demultiplexer_1_out7), .DataIN(reg4bits_6_datainrelay), .RegDATA(reg4bits_7_regdata));  // open: DataINRelay
  Multiplexer #(.select(3), .width(4), .enable("false")) multiplexer_1 (
    .in0(4'b0000), .in1(reg4bits_1_regdata), .in2(reg4bits_2_regdata), .in3(reg4bits_3_regdata),
    .in4(reg4bits_4_regdata), .in5(reg4bits_5_regdata), .in6(reg4bits_6_regdata), .in7(reg4bits_7_regdata),
    .out(DataX), .sel(DataRegX));
  Multiplexer #(.select(3), .width(4), .enable("false")) multiplexer_2 (
    .in0(4'b0000), .in1(reg4bits_1_regdata), .in2(reg4bits_2_regdata), .in3(reg4bits_3_regdata),
    .in4(reg4bits_4_regdata), .in5(reg4bits_5_regdata), .in6(reg4bits_6_regdata), .in7(reg4bits_7_regdata),
    .out(DataY), .sel(DataRegY));
  Hex_Digit_Display hex_digit_display_2 (.value(DataX));  // open: dp
  Hex_Digit_Display hex_digit_display_3 (.value(DataY));  // open: dp
endmodule

module BRsimples (
  input  [3:0] in_1,
  input  in_2,
  input  in_3,
  input  in_4,
  input  in_5,
  input  in_6,
  input  in_7,
  input  in_8,
  input  in_9
);

  wire [3:0] reg4bits_1_datainrelay, reg4bits_1_regdata, reg4bits_2_datainrelay, reg4bits_2_regdata,
       reg4bits_3_datainrelay, reg4bits_3_regdata, reg4bits_4_datainrelay, reg4bits_4_regdata,
       reg4bits_5_datainrelay, reg4bits_6_datainrelay, reg4bits_7_datainrelay;

  Hex_Digit_Display hex_digit_display_1 (.value(in_1));  // open: dp
  reg4bits reg4bits_1 (.WR(in_2), .DataIN(in_1), .DataINRelay(reg4bits_1_datainrelay), .RegDATA(reg4bits_1_regdata));
  reg4bits reg4bits_2 (
    .WR(in_3), .DataIN(reg4bits_1_datainrelay), .DataINRelay(reg4bits_2_datainrelay),
    .RegDATA(reg4bits_2_regdata));
  reg4bits reg4bits_3 (
    .WR(in_4), .DataIN(reg4bits_2_datainrelay), .DataINRelay(reg4bits_3_datainrelay),
    .RegDATA(reg4bits_3_regdata));
  reg4bits reg4bits_4 (
    .WR(in_5), .DataIN(reg4bits_3_datainrelay), .DataINRelay(reg4bits_4_datainrelay),
    .RegDATA(reg4bits_4_regdata));
  reg4bits reg4bits_5 (
    .WR(in_6), .DataIN(reg4bits_4_datainrelay), .DataINRelay(reg4bits_5_datainrelay));  // open: RegDATA
  reg4bits reg4bits_6 (
    .WR(in_7), .DataIN(reg4bits_5_datainrelay), .DataINRelay(reg4bits_6_datainrelay));  // open: RegDATA
  reg4bits reg4bits_7 (
    .WR(in_8), .DataIN(reg4bits_6_datainrelay), .DataINRelay(reg4bits_7_datainrelay));  // open: RegDATA
  reg4bits reg4bits_8 (.WR(in_9), .DataIN(reg4bits_7_datainrelay));  // open: DataINRelay, RegDATA
  Hex_Digit_Display hex_digit_display_2 (.value(reg4bits_1_regdata));  // open: dp
  Hex_Digit_Display hex_digit_display_3 (.value(reg4bits_2_regdata));  // open: dp
  Hex_Digit_Display hex_digit_display_4 (.value(reg4bits_3_regdata));  // open: dp
  Hex_Digit_Display hex_digit_display_5 (.value(reg4bits_4_regdata));  // open: dp
endmodule

module ULA (
  input  [3:0] A,
  input  [3:0] B,
  input  [1:0] OpCode,
  output [3:0] ULA__Result
);

  wire [3:0] adder_1_out, and_1_out, or_1_out;

  assign and_1_out = A & B;  // AND_Gate and_1, 4 bits wide
  assign or_1_out = A | B;  // OR_Gate or_1, 4 bits wide
  Adder #(.width(4)) adder_1 (.a(A), .b(B), .out(adder_1_out), .cin(1'b0));  // open: cout
  Multiplexer #(.select(2), .width(4), .enable("false")) multiplexer_1 (
    .in0(and_1_out), .in1(or_1_out), .in2(adder_1_out), .in3(4'b0000), .out(ULA__Result), .sel(OpCode));
endmodule
