// Logisim project Projeto (1).circ as structural Verilog
// +
module Somador (
  input  A,
  input  B,
  input  Vem1,
  output Soma,
  output Vai1
);

  wire and_1_out, and_2_out, and_3_out, xor_1_out;

  xor xor_1 (xor_1_out, A, B);
  and and_1 (and_1_out, A, B);
  and and_2 (and_2_out, A, Vem1);
  and and_3 (and_3_out, B, Vem1);
  xor xor_2 (Soma, xor_1_out, Vem1);
  or or_1 (Vai1, and_1_out, and_2_out, and_3_out);
endmodule

module Mux2 (
  input  A,
  input  B,
  input  Sel1,
  output S
);

  wire and_1_out, and_2_out;

  and and_1 (and_1_out, A, ~Sel1);  // AND_Gate
  and and_2 (and_2_out, B, Sel1);
  or or_1 (S, and_1_out, and_2_out);
endmodule

module Mux4 (
  input  A,
  input  B,
  input  C,
  input  D,
  input  in_5,
  input  in_6,
  output S
);

  wire and_1_out, and_2_out, and_3_out, and_4_out;

  and and_1 (and_1_out, A, ~in_5, ~in_6);  // AND_Gate
  and and_2 (and_2_out, B, ~in_5, in_6);  // AND_Gate
  and and_3 (and_3_out, C, in_5, ~in_6);  // AND_Gate
  and and_4 (and_4_out, D, in_5, in_6);
  or or_1 (S, and_1_out, and_2_out, and_3_out, and_4_out);
endmodule

module Mux8 (
  input  A,
  input  B,
  input  C,
  input  D,
  input  E,
  input  F,
  input  G,
  input  H,
  input  Sel0,
  input  Sel1,
  input  Sel2,
  output S
);

  wire and_1_out, and_2_out, and_3_out, and_4_out, and_5_out, and_6_out, and_7_out, and_8_out;

  and and_1 (and_1_out, A, ~Sel0, ~Sel1, ~Sel2);  // AND_Gate
  and and_2 (and_2_out, B, ~Sel0, ~Sel1, Sel2);  // AND_Gate
  and and_3 (and_3_out, C, ~Sel0, Sel1, ~Sel2);  // AND_Gate
  and and_4 (and_4_out, D, ~Sel0, Sel1, Sel2);  // AND_Gate
  and and_5 (and_5_out, E, Sel0, ~Sel1, ~Sel2);  // AND_Gate
  and and_6 (and_6_out, F, Sel0, ~Sel1, Sel2);  // AND_Gate
  and and_7 (and_7_out, G, Sel0, Sel1, ~Sel2);  // AND_Gate
  and and_8 (and_8_out, H, Sel0, Sel1, Sel2);
  or or_1 (S, and_1_out, and_2_out, and_3_out, and_4_out, and_5_out, and_6_out, and_7_out, and_8_out);
endmodule

module Mux16 (
  input  A,
  input  B,
  input  C,
  input  D,
  input  E,
  input  F,
  input  G,
  input  H,
  input  I,
  input  J,
  input  K,
  input  L,
  input  M,
  input  N,
  input  O,
  input  P,
  input  Sel0,
  input  Sel1,
  input  Sel2,
  input  Sel3,
  output S
);

  wire and_1_out, and_2_out, and_3_out, and_4_out, and_5_out, and_6_out, and_7_out, and_8_out, and_9_out,
       and_10_out, and_11_out, and_12_out, and_13_out, and_14_out, and_15_out, and_16_out;

  and and_1 (and_1_out, A, ~Sel0, ~Sel1, ~Sel2, ~Sel3);  // AND_Gate
  and and_2 (and_2_out, B, ~Sel0, ~Sel1, ~Sel2, Sel3);  // AND_Gate
  and and_3 (and_3_out, C, ~Sel0, ~Sel1, Sel2, ~Sel3);  // AND_Gate
  and and_4 (and_4_out, D, ~Sel0, ~Sel1, Sel2, Sel3);  // AND_Gate
  and and_5 (and_5_out, E, ~Sel0, Sel1, ~Sel2, ~Sel3);  // AND_Gate
  and and_6 (and_6_out, F, ~Sel0, Sel1, ~Sel2, Sel3);  // AND_Gate
  and and_7 (and_7_out, G, ~Sel0, Sel1, Sel2, ~Sel3);  // AND_Gate
  and and_8 (and_8_out, H, ~Sel0, Sel1, Sel2, Sel3);  // AND_Gate
  and and_9 (and_9_out, I, Sel0, ~Sel1, ~Sel2, ~Sel3);  // AND_Gate
  and and_10 (and_10_out, J, Sel0, ~Sel1, ~Sel2, Sel3);  // AND_Gate
  and and_11 (and_11_out, K, Sel0, ~Sel1, Sel2, ~Sel3);  // AND_Gate
  and and_12 (and_12_out, L, Sel0, ~Sel1, Sel2, Sel3);  // AND_Gate
  and and_13 (and_13_out, M, Sel0, Sel1, ~Sel2, ~Sel3);  // AND_Gate
  and and_14 (and_14_out, N, Sel0, Sel1, ~Sel2, Sel3);  // AND_Gate
  and and_15 (and_15_out, O, Sel0, Sel1, Sel3, ~Sel3);  // AND_Gate
  and and_16 (and_16_out, P, Sel0, Sel1, Sel2, Sel3);
  or or_1 (S, and_1_out, and_2_out, and_3_out, and_4_out, and_5_out, and_6_out, and_7_out, and_8_out, and_9_out, and_10_out, and_11_out, and_12_out, and_13_out, and_14_out, and_15_out, and_16_out);
endmodule

module Mux32_com_Mux16 (
  input  E0,
  input  E16,
  input  E1,
  input  E17,
  input  E2,
  input  E18,
  input  E3,
  input  E19,
  input  E4,
  input  E20,
  input  E5,
  input  E21,
  input  E6,
  input  E22,
  input  E7,
  input  E23,
  input  E8,
  input  E24,
  input  E9,
  input  E25,
  input  E10,
  input  E26,
  input  E11,
  input  E27,
  input  E12,
  input  E28,
  input  E13,
  input  E29,
  input  E14,
  input  E30,
  input  E15,
  input  E31,
  input  in_33,
  input  in_34,
  input  in_35,
  input  in_36,
  input  in_37,
  output S
);

  wire mux16_1_s, mux16_2_s;

  Mux16 mux16_1 (
    .A(E0), .B(E1), .C(E2), .D(E3), .E(E4), .F(E5), .G(E6), .H(E7), .I(E8), .J(E9), .K(E10), .L(E11),
    .M(E12), .N(E13), .O(E14), .P(E15), .Sel0(in_33), .Sel1(in_34), .Sel2(in_35), .Sel3(in_36), .S(mux16_1_s));
  Mux8 mux8_1 (
    .A(mux16_1_s), .B(mux16_2_s), .C(1'b0), .D(1'b0), .E(1'b0), .F(1'b0), .G(1'b0), .H(1'b0), .Sel0(in_37),
    .Sel1(in_37), .Sel2(in_37), .S(S));
  Mux16 mux16_2 (
    .A(E16), .B(E17), .C(E18), .D(E19), .E(E20), .F(E21), .G(E22), .H(E23), .I(E24), .J(E25), .K(E26),
    .L(E27), .M(E28), .N(E29), .O(E30), .P(E31), .Sel0(in_33), .Sel1(in_34), .Sel2(in_35), .Sel3(in_36),
    .S(mux16_2_s));
endmodule

// ULA
module ALUcell (
  input  A,
  input  B,
  input  Vem1,
  input  Bin,
  input  C0,
  input  C1,
  input  C2,
  input  C3,
  input  C4,
  output S,
  output Vai1,
  output Bout
);

  wire and_1_out, nand_1_out, or_1_out, somador_1_soma, subtrator_1_sub, xor_1_out;

  and and_1 (and_1_out, A, B);
  or or_1 (or_1_out, A, B);
  xor xor_1 (xor_1_out, A, B);
  Somador somador_1 (.Soma(somador_1_soma), .Vai1(Vai1), .A(A), .B(B), .Vem1(Vem1));
  nand nand_1 (nand_1_out, A, B);
  Subtrator subtrator_1 (.A(A), .B(B), .Bin(Bin), .Sub(subtrator_1_sub), .Bout(Bout));
  Mux32_com_Mux16 mux32_com_mux16_1 (
    .E0(and_1_out), .E16(1'b0), .E1(or_1_out), .E17(1'b0), .E2(xor_1_out), .E18(1'b0), .E3(somador_1_soma),
    .E19(1'b0), .E4(somador_1_soma), .E20(1'b0), .E5(nand_1_out), .E21(1'b0), .E6(subtrator_1_sub),
    .E22(1'b0), .E7(1'b0), .E23(1'b0), .E8(1'b0), .E24(1'b0), .E9(1'b0), .E25(1'b0), .E10(1'b0), .E26(1'b0),
    .E11(1'b0), .E27(1'b0), .E12(1'b0), .E28(1'b0), .E13(1'b0), .E29(1'b0), .E14(1'b0), .E30(1'b0),
    .E15(1'b0), .E31(1'b0), .in_37(C0), .in_33(C1), .in_34(C2), .in_35(C3), .S(S), .in_36(C4));
endmodule

// -
module Subtrator (
  input  A,
  input  B,
  input  Bin,
  output Sub,
  output Bout
);

  wire and_1_out, and_2_out, and_3_out, xor_1_out;

  xor xor_1 (xor_1_out, A, B);
  and and_1 (and_1_out, B, Bin);
  and and_2 (and_2_out, ~A, Bin);  // AND_Gate
  and and_3 (and_3_out, ~A, B);  // AND_Gate
  xor xor_2 (Sub, xor_1_out, Bin);
  and and_4 (Bout, and_1_out, and_2_out, and_3_out);
endmodule

module ULA (
  input  Carry_In,
  input  A,
  input  B,
  input  Carry_Out,
  input  c0,
  input  c1,
  input  c2,
  input  c3,
  input  c4,
  output out_10
);

  wire and_1_out, nand_1_out, nor_1_out, or_1_out, somador_1_soma;

  and and_1 (and_1_out, A, B);
  or or_1 (or_1_out, A, B);
  nor nor_1 (nor_1_out, A, B);
  nand nand_1 (nand_1_out, A, B);
  Somador somador_1 (.Soma(somador_1_soma), .Vai1(Carry_Out), .A(A), .B(B), .Vem1(Carry_In));
  Mux32_com_Mux16 mux32_com_mux16_1 (
    .E0(and_1_out), .E16(1'b0), .E1(or_1_out), .E17(1'b0), .E2(nor_1_out), .E18(1'b0), .E3(nand_1_out),
    .E19(1'b0), .E4(somador_1_soma), .E20(1'b0), .E5(somador_1_soma), .E21(1'b0), .E6(1'b0), .E22(1'b0),
    .E7(1'b0), .E23(1'b0), .E8(1'b0), .E24(1'b0), .E9(1'b0), .E25(1'b0), .E10(1'b0), .E26(1'b0), .E11(1'b0),
    .E27(1'b0), .E12(1'b0), .E28(1'b0), .E13(1'b0), .E29(1'b0), .E14(1'b0), .E30(1'b0), .E15(1'b0),
    .E31(1'b0), .in_37(c0), .in_33(c1), .in_34(c2), .in_35(c3), .S(out_10), .in_36(c4));
endmodule

module Processador_Teste (
  input  [31:0] B,
  input  C0,
  input  C1,
  input  C2,
  input  C3,
  input  C4,
  input  [31:0] in_7,
  input  [31:0] \Saída 
);

  wire undriven, undriven_2, undriven_3, undriven_4, undriven_5, undriven_6, undriven_7, undriven_8,
       undriven_9, undriven_10, undriven_11, undriven_12, undriven_13, undriven_14, undriven_15, undriven_16,
       undriven_17, undriven_18, undriven_19, undriven_20, undriven_21, undriven_22, undriven_23,
       undriven_24, undriven_25, undriven_26, undriven_27, undriven_28, undriven_29, undriven_30, undriven_31;

  ULA _0 (
    .Carry_In(1'b0), .A(in_7[0]), .B(B[0]), .Carry_Out(undriven), .c0(C0), .c1(C1), .c2(C2), .c3(C3), .c4(C4));  // open: out_10
  ULA _8 (
    .Carry_In(undriven_29), .A(in_7[8]), .B(B[8]), .Carry_Out(undriven_2), .c0(C0), .c1(C1), .c2(C2),
    .c3(C3), .c4(C4));  // open: out_10
  ULA _16 (
    .Carry_In(undriven_30), .A(in_7[16]), .B(B[16]), .Carry_Out(undriven_3), .c0(C0), .c1(C1), .c2(C2),
    .c3(C3), .c4(C4));  // open: out_10
  ULA _24 (
    .Carry_In(undriven_31), .A(in_7[24]), .B(B[24]), .Carry_Out(undriven_4), .c0(C0), .c1(C1), .c2(C2),
    .c3(C3), .c4(C4));  // open: out_10
  ULA _1 (
    .Carry_In(undriven), .A(in_7[1]), .B(B[1]), .Carry_Out(undriven_5), .c0(C0), .c1(C1), .c2(C2), .c3(C3),
    .c4(C4));  // open: out_10
  ULA _9 (
    .Carry_In(undriven_2), .A(in_7[9]), .B(B[9]), .Carry_Out(undriven_6), .c0(C0), .c1(C1), .c2(C2), .c3(C3),
    .c4(C4));  // open: out_10
  ULA _17 (
    .Carry_In(undriven_3), .A(in_7[17]), .B(B[17]), .Carry_Out(undriven_7), .c0(C0), .c1(C1), .c2(C2),
    .c3(C3), .c4(C4));  // open: out_10
  ULA _25 (
    .Carry_In(undriven_4), .A(in_7[25]), .B(B[25]), .Carry_Out(undriven_8), .c0(C0), .c1(C1), .c2(C2),
    .c3(C3), .c4(C4));  // open: out_10
  ULA _2 (
    .Carry_In(undriven_5), .A(in_7[2]), .B(B[2]), .Carry_Out(undriven_9), .c0(C0), .c1(C1), .c2(C2), .c3(C3),
    .c4(C4));  // open: out_10
  ULA _10 (
    .Carry_In(undriven_6), .A(in_7[10]), .B(B[10]), .Carry_Out(undriven_10), .c0(C0), .c1(C1), .c2(C2),
    .c3(C3), .c4(C4));  // open: out_10
  ULA _18 (
    .Carry_In(undriven_7), .A(in_7[18]), .B(B[18]), .Carry_Out(undriven_11), .c0(C0), .c1(C1), .c2(C2),
    .c3(C3), .c4(C4));  // open: out_10
  ULA _26 (
    .Carry_In(undriven_8), .A(in_7[26]), .B(B[26]), .Carry_Out(undriven_12), .c0(C0), .c1(C1), .c2(C2),
    .c3(C3), .c4(C4));  // open: out_10
  ULA _3 (
    .Carry_In(undriven_9), .A(in_7[3]), .B(B[3]), .Carry_Out(undriven_13), .c0(C0), .c1(C1), .c2(C2),
    .c3(C3), .c4(C4));  // open: out_10
  ULA _11 (
    .Carry_In(undriven_10), .A(in_7[11]), .B(B[11]), .Carry_Out(undriven_14), .c0(C0), .c1(C1), .c2(C2),
    .c3(C3), .c4(C4));  // open: out_10
  ULA _19 (
    .Carry_In(undriven_11), .A(in_7[19]), .B(B[19]), .Carry_Out(undriven_15), .c0(C0), .c1(C1), .c2(C2),
    .c3(C3), .c4(C4));  // open: out_10
  ULA _27 (
    .Carry_In(undriven_12), .A(in_7[27]), .B(B[27]), .Carry_Out(undriven_16), .c0(C0), .c1(C1), .c2(C2),
    .c3(C3), .c4(C4));  // open: out_10
  ULA _4 (
    .Carry_In(undriven_13), .A(in_7[4]), .B(B[4]), .Carry_Out(undriven_17), .c0(C0), .c1(C1), .c2(C2),
    .c3(C3), .c4(C4));  // open: out_10
  ULA _12 (
    .Carry_In(undriven_14), .A(in_7[12]), .B(B[12]), .Carry_Out(undriven_18), .c0(C0), .c1(C1), .c2(C2),
    .c3(C3), .c4(C4));  // open: out_10
  ULA _20 (
    .Carry_In(undriven_15), .A(in_7[20]), .B(B[20]), .Carry_Out(undriven_19), .c0(C0), .c1(C1), .c2(C2),
    .c3(C3), .c4(C4));  // open: out_10
  ULA _28 (
    .Carry_In(undriven_16), .A(in_7[28]), .B(B[28]), .Carry_Out(undriven_20), .c0(C0), .c1(C1), .c2(C2),
    .c3(C3), .c4(C4));  // open: out_10
  ULA _5 (
    .Carry_In(undriven_17), .A(in_7[5]), .B(B[5]), .Carry_Out(undriven_21), .c0(C0), .c1(C1), .c2(C2),
    .c3(C3), .c4(C4));  // open: out_10
  ULA _13 (
    .Carry_In(undriven_18), .A(in_7[13]), .B(B[13]), .Carry_Out(undriven_22), .c0(C0), .c1(C1), .c2(C2),
    .c3(C3), .c4(C4));  // open: out_10
  ULA _21 (
    .Carry_In(undriven_19), .A(in_7[21]), .B(B[21]), .Carry_Out(undriven_23), .c0(C0), .c1(C1), .c2(C2),
    .c3(C3), .c4(C4));  // open: out_10
  ULA _29 (
    .Carry_In(undriven_20), .A(in_7[29]), .B(B[29]), .Carry_Out(undriven_24), .c0(C0), .c1(C1), .c2(C2),
    .c3(C3), .c4(C4));  // open: out_10
  ULA _6 (
    .Carry_In(undriven_21), .A(in_7[6]), .B(B[6]), .Carry_Out(undriven_25), .c0(C0), .c1(C1), .c2(C2),
    .c3(C3), .c4(C4));  // open: out_10
  ULA _14 (
    .Carry_In(undriven_22), .A(in_7[14]), .B(B[14]), .Carry_Out(undriven_26), .c0(C0), .c1(C1), .c2(C2),
    .c3(C3), .c4(C4));  // open: out_10
  ULA _22 (
    .Carry_In(undriven_23), .A(in_7[22]), .B(B[22]), .Carry_Out(undriven_27), .c0(C0), .c1(C1), .c2(C2),
    .c3(C3), .c4(C4));  // open: out_10
  ULA _30 (
    .Carry_In(undriven_24), .A(in_7[30]), .B(B[30]), .Carry_Out(undriven_28), .c0(C0), .c1(C1), .c2(C2),
    .c3(C3), .c4(C4));  // open: out_10
  ULA _7 (
    .Carry_In(undriven_25), .A(in_7[7]), .B(B[7]), .Carry_Out(undriven_29), .c0(C0), .c1(C1), .c2(C2),
    .c3(C3), .c4(C4));  // open: out_10
  ULA _15 (
    .Carry_In(undriven_26), .A(in_7[15]), .B(B[15]), .Carry_Out(undriven_30), .c0(C0), .c1(C1), .c2(C2),
    .c3(C3), .c4(C4));  // open: out_10
  ULA _23 (
    .Carry_In(undriven_27), .A(in_7[23]), .B(B[23]), .Carry_Out(undriven_31), .c0(C0), .c1(C1), .c2(C2),
    .c3(C3), .c4(C4));  // open: out_10
  ULA _31 (
    .Carry_In(undriven_28), .A(in_7[31]), .B(B[31]), .Carry_Out(1'b0), .c0(C0), .c1(C1), .c2(C2), .c3(C3),
    .c4(C4));  // open: out_10
endmodule

module Registrador (
  input  [31:0] in_1,
  input  WR,
  input  [31:0] in_3
);

  wire [22:0] _0_q;

  D_Flip_Flop _0 (.clk(WR), .D(in_1[0]), .Q(_0_q[0]));  // open: Qn, preset, en, reset
  D_Flip_Flop _8 (.clk(WR), .D(in_1[8]), .Q(_0_q[7]));  // open: Qn, preset, en, reset
  D_Flip_Flop _16 (.clk(WR), .D(in_1[16]), .Q(_0_q[15]));  // open: Qn, preset, en, reset
  D_Flip_Flop _24 (.clk(WR), .D(in_1[24]));  // open: Q, Qn, preset, en, reset
  D_Flip_Flop _1 (.clk(WR), .D(in_1[1]), .Q(_0_q[1]));  // open: Qn, preset, en, reset
  D_Flip_Flop _9 (.clk(WR), .D(in_1[9]), .Q(_0_q[8]));  // open: Qn, preset, en, reset
  D_Flip_Flop _17 (.clk(WR), .D(in_1[17]), .Q(_0_q[16]));  // open: Qn, preset, en, reset
  D_Flip_Flop _25 (.clk(WR), .D(in_1[25]));  // open: Q, Qn, preset, en, reset
  D_Flip_Flop _2 (.clk(WR), .D(in_1[2]), .Q(_0_q[2]));  // open: Qn, preset, en, reset
  D_Flip_Flop _10 (.clk(WR), .D(in_1[10]), .Q(_0_q[9]));  // open: Qn, preset, en, reset
  D_Flip_Flop _18 (.clk(WR), .D(in_1[18]), .Q(_0_q[17]));  // open: Qn, preset, en, reset
  D_Flip_Flop _26 (.clk(WR), .D(in_1[26]));  // open: Q, Qn, preset, en, reset
  D_Flip_Flop _3 (.clk(WR), .D(in_1[3]));  // open: Q, Qn, preset, en, reset
  D_Flip_Flop _11 (.clk(WR), .D(in_1[11]), .Q(_0_q[10]));  // open: Qn, preset, en, reset
  D_Flip_Flop _19 (.clk(WR), .D(in_1[19]), .Q(_0_q[18]));  // open: Qn, preset, en, reset
  D_Flip_Flop _27 (.clk(WR), .D(in_1[27]));  // open: Q, Qn, preset, en, reset
  D_Flip_Flop _4 (.clk(WR), .D(in_1[4]), .Q(_0_q[3]));  // open: Qn, preset, en, reset
  D_Flip_Flop _12 (.clk(WR), .D(in_1[12]), .Q(_0_q[11]));  // open: Qn, preset, en, reset
  D_Flip_Flop _20 (.clk(WR), .D(in_1[20]), .Q(_0_q[19]));  // open: Qn, preset, en, reset
  D_Flip_Flop _28 (.clk(WR), .D(in_1[28]));  // open: Q, Qn, preset, en, reset
  D_Flip_Flop _5 (.clk(WR), .D(in_1[5]), .Q(_0_q[4]));  // open: Qn, preset, en, reset
  D_Flip_Flop _13 (.clk(WR), .D(in_1[13]), .Q(_0_q[12]));  // open: Qn, preset, en, reset
  D_Flip_Flop _21 (.clk(WR), .D(in_1[21]), .Q(_0_q[20]));  // open: Qn, preset, en, reset
  D_Flip_Flop _29 (.clk(WR), .D(in_1[29]));  // open: Q, Qn, preset, en, reset
  D_Flip_Flop _6 (.clk(WR), .D(in_1[6]), .Q(_0_q[5]));  // open: Qn, preset, en, reset
  D_Flip_Flop _14 (.clk(WR), .D(in_1[14]), .Q(_0_q[13]));  // open: Qn, preset, en, reset
  D_Flip_Flop _22 (.clk(WR), .D(in_1[22]), .Q(_0_q[21]));  // open: Qn, preset, en, reset
  D_Flip_Flop _30 (.clk(WR), .D(in_1[30]));  // open: Q, Qn, preset, en, reset
  D_Flip_Flop _7 (.clk(WR), .D(in_1[7]), .Q(_0_q[6]));  // open: Qn, preset, en, reset
  D_Flip_Flop _15 (.clk(WR), .D(in_1[15]), .Q(_0_q[14]));  // open: Qn, preset, en, reset
  D_Flip_Flop _23 (.clk(WR), .D(in_1[23]), .Q(_0_q[22]));  // open: Qn, preset, en, reset
  D_Flip_Flop _31 (.clk(WR), .D(in_1[31]));  // open: Q, Qn, preset, en, reset

  assign in_3 = in_1;
endmodule
