// Logisim project Projeto.circ as structural Verilog
// +
module Somador (
  input  A,
  input  B,
  input  Vem1,
  output Soma,
  output Vai1
);

  wire and_1_out, and_2_out, and_3_out, xor_1_out;

  xor xor_1 (xor_1_out, A, B);
  and and_1 (and_1_out, A, B);
  and and_2 (and_2_out, A, Vem1);
  and and_3 (and_3_out, B, Vem1);
  xor xor_2 (Soma, xor_1_out, Vem1);
  or or_1 (Vai1, and_1_out, and_2_out, and_3_out);
endmodule

module Mux2 (
  input  A,
  input  B,
  input  Sel1,
  output S
);

  wire and_1_out, and_2_out;

  and and_1 (and_1_out, A, ~Sel1);  // AND_Gate
  and and_2 (and_2_out, B, Sel1);
  or or_1 (S, and_1_out, and_2_out);
endmodule

module Mux4 (
  input  A,
  input  B,
  input  C,
  input  D,
  input  in_5,
  input  in_6,
  output S
);

  wire and_1_out, and_2_out, and_3_out, and_4_out;

  and and_1 (and_1_out, A, ~in_5, ~in_6);  // AND_Gate
  and and_2 (and_2_out, B, ~in_5, in_6);  // AND_Gate
  and and_3 (and_3_out, C, in_5, ~in_6);  // AND_Gate
  and and_4 (and_4_out, D, in_5, in_6);
  or or_1 (S, and_1_out, and_2_out, and_3_out, and_4_out);
endmodule

module Mux4_com_mux2 (
  input  A,
  input  B,
  input  C,
  input  D,
  input  Sel0,
  input  Sel1,
  output out_7
);

  wire mux2_1_s, mux2_2_s;

  Mux2 mux2_1 (.A(A), .B(B), .Sel1(Sel0), .S(mux2_1_s));
  Mux2 mux2_2 (.A(C), .B(D), .Sel1(Sel0), .S(mux2_2_s));
  Mux2 mux2_3 (.A(mux2_1_s), .B(mux2_2_s), .Sel1(Sel1), .S(out_7));
endmodule

module Mux8 (
  input  A,
  input  B,
  input  C,
  input  D,
  input  E,
  input  F,
  input  G,
  input  H,
  input  Sel0,
  input  Sel1,
  input  Sel2,
  output S
);

  wire and_1_out, and_2_out, and_3_out, and_4_out, and_5_out, and_6_out, and_7_out, and_8_out;

  and and_1 (and_1_out, A, ~Sel0, ~Sel1, ~Sel2);  // AND_Gate
  and and_2 (and_2_out, B, ~Sel0, ~Sel1, Sel2);  // AND_Gate
  and and_3 (and_3_out, C, ~Sel0, Sel1, ~Sel2);  // AND_Gate
  and and_4 (and_4_out, D, ~Sel0, Sel1, Sel2);  // AND_Gate
  and and_5 (and_5_out, E, Sel0, ~Sel1, ~Sel2);  // AND_Gate
  and and_6 (and_6_out, F, Sel0, ~Sel1, Sel2);  // AND_Gate
  and and_7 (and_7_out, G, Sel0, Sel1, ~Sel2);  // AND_Gate
  and and_8 (and_8_out, H, Sel0, Sel1, Sel2);
  or or_1 (S, and_1_out, and_2_out, and_3_out, and_4_out, and_5_out, and_6_out, and_7_out, and_8_out);
endmodule

module Mux8_com_Mux4 (
  input  A,
  input  B,
  input  C,
  input  D,
  input  E,
  input  F,
  input  G,
  input  H,
  input  Sel0,
  input  Sel1,
  input  Sel2,
  output S
);

  wire mux4_1_s, mux4_2_s;

  Mux4 mux4_1 (.A(A), .B(B), .C(C), .D(D), .in_5(Sel0), .in_6(Sel1), .S(mux4_1_s));
  Mux4 mux4_2 (.A(E), .B(F), .C(G), .D(H), .in_5(Sel0), .in_6(Sel1), .S(mux4_2_s));
  Mux4 mux4_3 (.A(mux4_1_s), .B(mux4_2_s), .C(1'b0), .D(1'b0), .in_5(Sel2), .in_6(Sel2), .S(S));
endmodule

module Mux16 (
  input  A,
  input  B,
  input  C,
  input  D,
  input  E,
  input  F,
  input  G,
  input  H,
  input  I,
  input  J,
  input  K,
  input  L,
  input  M,
  input  N,
  input  O,
  input  P,
  input  Sel0,
  input  Sel1,
  input  Sel2,
  input  Sel3,
  output S
);

  wire and_1_out, and_2_out, and_3_out, and_4_out, and_5_out, and_6_out, and_7_out, and_8_out, and_9_out,
       and_10_out, and_11_out, and_12_out, and_13_out, and_14_out, and_15_out, and_16_out;

  and and_1 (and_1_out, A, ~Sel0, ~Sel1, ~Sel2, ~Sel3);  // AND_Gate
  and and_2 (and_2_out, B, ~Sel0, ~Sel1, ~Sel2, Sel3);  // AND_Gate
  and and_3 (and_3_out, C, ~Sel0, ~Sel1, Sel2, ~Sel3);  // AND_Gate
  and and_4 (and_4_out, D, ~Sel0, ~Sel1, Sel2, Sel3);  // AND_Gate
  and and_5 (and_5_out, E, ~Sel0, Sel1, ~Sel2, ~Sel3);  // AND_Gate
  and and_6 (and_6_out, F, ~Sel0, Sel1, ~Sel2, Sel3);  // AND_Gate
  and and_7 (and_7_out, G, ~Sel0, Sel1, Sel2, ~Sel3);  // AND_Gate
  and and_8 (and_8_out, H, ~Sel0, Sel1, Sel2, Sel3);  // AND_Gate
  and and_9 (and_9_out, I, Sel0, ~Sel1, ~Sel2, ~Sel3);  // AND_Gate
  and and_10 (and_10_out, J, Sel0, ~Sel1, ~Sel2, Sel3);  // AND_Gate
  and and_11 (and_11_out, K, Sel0, ~Sel1, Sel2, ~Sel3);  // AND_Gate
  and and_12 (and_12_out, L, Sel0, ~Sel1, Sel2, Sel3);  // AND_Gate
  and and_13 (and_13_out, M, Sel0, Sel1, ~Sel2, ~Sel3);  // AND_Gate
  and and_14 (and_14_out, N, Sel0, Sel1, ~Sel2, Sel3);  // AND_Gate
  and and_15 (and_15_out, O, Sel0, Sel1, Sel3, ~Sel3);  // AND_Gate
  and and_16 (and_16_out, P, Sel0, Sel1, Sel2, Sel3);
  or or_1 (S, and_1_out, and_2_out, and_3_out, and_4_out, and_5_out, and_6_out, and_7_out, and_8_out, and_9_out, and_10_out, and_11_out, and_12_out, and_13_out, and_14_out, and_15_out, and_16_out);
endmodule

module Mux16_com_Mux8 (
  input  A,
  input  B,
  input  C,
  input  D,
  input  E,
  input  F,
  input  G,
  input  H,
  input  I,
  input  J,
  input  K,
  input  L,
  input  L_2,
  input  L_3,
  input  L_4,
  input  P,
  input  in_17,
  input  in_18,
  input  in_19,
  input  in_20,
  input  M,
  input  N,
  input  O,
  output S
);

  wire mux8_1_s, mux8_2_s;

  Mux8 mux8_1 (
    .A(A), .B(B), .C(C), .D(D), .E(E), .F(F), .G(G), .H(H), .Sel0(in_17), .Sel1(in_18), .Sel2(in_19),
    .S(mux8_1_s));
  Mux8 mux8_2 (
    .A(I), .B(J), .C(K), .D(L), .E(L_2), .F(L_3), .G(L_4), .H(P), .Sel0(in_17), .Sel1(in_18), .Sel2(in_19),
    .S(mux8_2_s));
  Mux8 mux8_3 (
    .A(mux8_1_s), .B(mux8_2_s), .C(1'b0), .D(1'b0), .E(1'b0), .F(1'b0), .G(1'b0), .H(1'b0), .Sel0(in_20),
    .Sel1(in_20), .Sel2(in_20), .S(S));
endmodule

module Mux32_com_Mux16 (
  input  E0,
  input  E16,
  input  E1,
  input  E17,
  input  E2,
  input  E18,
  input  E3,
  input  E19,
  input  E4,
  input  E20,
  input  E5,
  input  E21,
  input  E6,
  input  E22,
  input  E7,
  input  E23,
  input  E8,
  input  E24,
  input  E9,
  input  E25,
  input  E10,
  input  E26,
  input  E11,
  input  E27,
  input  E12,
  input  E28,
  input  E13,
  input  E29,
  input  E14,
  input  E30,
  input  E15,
  input  E31,
  input  in_33,
  input  in_34,
  input  in_35,
  input  in_36,
  input  in_37,
  output S
);

  wire mux16_1_s, mux16_2_s;

  Mux16 mux16_1 (
    .A(E0), .B(E1), .C(E2), .D(E3), .E(E4), .F(E5), .G(E6), .H(E7), .I(E8), .J(E9), .K(E10), .L(E11),
    .M(E12), .N(E13), .O(E14), .P(E15), .Sel0(in_33), .Sel1(in_34), .Sel2(in_35), .Sel3(in_36), .S(mux16_1_s));
  Mux8 mux8_1 (
    .A(mux16_1_s), .B(mux16_2_s), .C(1'b0), .D(1'b0), .E(1'b0), .F(1'b0), .G(1'b0), .H(1'b0), .Sel0(in_37),
    .Sel1(in_37), .Sel2(in_37), .S(S));
  Mux16 mux16_2 (
    .A(E16), .B(E17), .C(E18), .D(E19), .E(E20), .F(E21), .G(E22), .H(E23), .I(E24), .J(E25), .K(E26),
    .L(E27), .M(E28), .N(E29), .O(E30), .P(E31), .Sel0(in_33), .Sel1(in_34), .Sel2(in_35), .Sel3(in_36),
    .S(mux16_2_s));
endmodule

// ULA
module ALUcell (
  input  A,
  input  B,
  input  Vem1,
  input  Bin,
  input  C0,
  input  C1,
  input  C2,
  input  C3,
  input  C4,
  output S,
  output Vai1,
  output Bout
);

  wire and_1_out, nand_1_out, or_1_out, somador_1_soma, subtrator_1_sub, xor_1_out;

  and and_1 (and_1_out, A, B);
  or or_1 (or_1_out, A, B);
  xor xor_1 (xor_1_out, A, B);
  Somador somador_1 (.Soma(somador_1_soma), .Vai1(Vai1), .A(A), .B(B), .Vem1(Vem1));
  nand nand_1 (nand_1_out, A, B);
  Subtrator subtrator_1 (.A(A), .B(B), .Bin(Bin), .Sub(subtrator_1_sub), .Bout(Bout));
  Mux32_com_Mux16 mux32_com_mux16_1 (
    .E0(and_1_out), .E16(1'b0), .E1(or_1_out), .E17(1'b0), .E2(xor_1_out), .E18(1'b0), .E3(somador_1_soma),
    .E19(1'b0), .E4(somador_1_soma), .E20(1'b0), .E5(nand_1_out), .E21(1'b0), .E6(subtrator_1_sub),
    .E22(1'b0), .E7(and_1_out), .E23(1'b0), .E8(1'b0), .E24(1'b0), .E9(1'b0), .E25(1'b0), .E10(1'b0),
    .E26(1'b0), .E11(1'b0), .E27(1'b0), .E12(1'b0), .E28(1'b0), .E13(1'b0), .E29(1'b0), .E14(1'b0),
    .E30(1'b0), .E15(1'b0), .E31(1'b0), .in_37(C0), .in_33(C1), .in_34(C2), .in_35(C3), .S(S), .in_36(C4));
endmodule

// -
module Subtrator (
  input  A,
  input  B,
  input  Bin,
  output Sub,
  output Bout
);

  wire and_1_out, and_2_out, and_3_out, xor_1_out;

  xor xor_1 (xor_1_out, A, B);
  and and_1 (and_1_out, B, Bin);
  and and_2 (and_2_out, ~A, Bin);  // AND_Gate
  and and_3 (and_3_out, ~A, B);  // AND_Gate
  xor xor_2 (Sub, xor_1_out, Bin);
  and and_4 (Bout, and_1_out, and_2_out, and_3_out);
endmodule

// PROCESSADOR
module Processador (
  input  [4:0] OpCode,
  input  [31:0] A,
  input  Bin,
  input  [4:0] Shift_Amount,
  input  L_R,
  input  [31:0] B,
  output out_7,
  output [31:0] S,
  output out_9
);

  wire _0_bout, _0_vai1, _1_bout, _1_vai1, _2_bout, _2_vai1, _3_bout, _3_vai1, _4_bout, _4_vai1, _5_bout,
       _5_vai1, _6_bout, _6_vai1, _7_bout, _7_vai1, _8_bout, _8_vai1, _9_bout, _9_vai1, _10_bout, _10_vai1,
       _11_bout, _11_vai1, _12_bout, _12_vai1, _13_bout, _13_vai1, _14_bout, _14_vai1, _15_bout, _15_vai1,
       _16_bout, _16_vai1, _17_bout, _17_vai1, _18_bout, _18_vai1, _19_bout, _19_vai1, _20_bout, _20_vai1,
       _21_bout, _21_vai1, _22_bout, _22_vai1, _23_bout, _23_vai1, _24_bout, _24_vai1, _25_bout, _25_vai1,
       _26_bout, _26_vai1, _27_bout, _27_vai1, _28_bout, _28_vai1, _29_bout, _29_vai1, _30_bout, _30_vai1,
       _31_bout, _31_vai1, and_1_out, and_2_out, and_3_out, and_4_out, or_1_out, or_2_out;
  wire [31:0] deslocador_1_a_prime_b_prime;

  Deslocador deslocador_1 (.A_B(A), .A_prime_B_prime(deslocador_1_a_prime_b_prime), .in_2(L_R), .in_3(Shift_Amount));
  ALUcell _0 (
    .Vem1(1'b0), .Bin(Bin), .S(S[0]), .Vai1(_0_vai1), .Bout(_0_bout), .A(deslocador_1_a_prime_b_prime[0]),
    .B(B[0]), .C0(OpCode[4]), .C1(OpCode[3]), .C2(OpCode[2]), .C3(OpCode[1]), .C4(OpCode[0]));
  ALUcell _8 (
    .Vem1(_7_vai1), .Bin(_7_bout), .S(S[8]), .Vai1(_8_vai1), .Bout(_8_bout),
    .A(deslocador_1_a_prime_b_prime[8]), .B(B[8]), .C0(OpCode[4]), .C1(OpCode[3]), .C2(OpCode[2]),
    .C3(OpCode[1]), .C4(OpCode[0]));
  ALUcell _16 (
    .Vem1(_15_vai1), .Bin(_15_bout), .S(S[16]), .Vai1(_16_vai1), .Bout(_16_bout),
    .A(deslocador_1_a_prime_b_prime[16]), .B(B[16]), .C0(OpCode[4]), .C1(OpCode[3]), .C2(OpCode[2]),
    .C3(OpCode[1]), .C4(OpCode[0]));
  ALUcell _24 (
    .Vem1(_23_vai1), .Bin(_23_bout), .S(S[24]), .Vai1(_24_vai1), .Bout(_24_bout),
    .A(deslocador_1_a_prime_b_prime[24]), .B(B[24]), .C0(OpCode[4]), .C1(OpCode[3]), .C2(OpCode[2]),
    .C3(OpCode[1]), .C4(OpCode[0]));
  ALUcell _1 (
    .Vem1(_0_vai1), .Bin(_0_bout), .S(S[1]), .Vai1(_1_vai1), .Bout(_1_bout),
    .A(deslocador_1_a_prime_b_prime[1]), .B(B[1]), .C0(OpCode[4]), .C1(OpCode[3]), .C2(OpCode[2]),
    .C3(OpCode[1]), .C4(OpCode[0]));
  ALUcell _9 (
    .Vem1(_8_vai1), .Bin(_8_bout), .S(S[9]), .Vai1(_9_vai1), .Bout(_9_bout),
    .A(deslocador_1_a_prime_b_prime[9]), .B(B[9]), .C0(OpCode[4]), .C1(OpCode[3]), .C2(OpCode[2]),
    .C3(OpCode[1]), .C4(OpCode[0]));
  ALUcell _17 (
    .Vem1(_16_vai1), .Bin(_16_bout), .S(S[17]), .Vai1(_17_vai1), .Bout(_17_bout),
    .A(deslocador_1_a_prime_b_prime[17]), .B(B[17]), .C0(OpCode[4]), .C1(OpCode[3]), .C2(OpCode[2]),
    .C3(OpCode[1]), .C4(OpCode[0]));
  ALUcell _25 (
    .Vem1(_24_vai1), .Bin(_24_bout), .S(S[25]), .Vai1(_25_vai1), .Bout(_25_bout),
    .A(deslocador_1_a_prime_b_prime[25]), .B(B[25]), .C0(OpCode[4]), .C1(OpCode[3]), .C2(OpCode[2]),
    .C3(OpCode[1]), .C4(OpCode[0]));
  ALUcell _2 (
    .Vem1(_1_vai1), .Bin(_1_bout), .S(S[2]), .Vai1(_2_vai1), .Bout(_2_bout),
    .A(deslocador_1_a_prime_b_prime[2]), .B(B[2]), .C0(OpCode[4]), .C1(OpCode[3]), .C2(OpCode[2]),
    .C3(OpCode[1]), .C4(OpCode[0]));
  ALUcell _10 (
    .Vem1(_9_vai1), .Bin(_9_bout), .S(S[10]), .Vai1(_10_vai1), .Bout(_10_bout),
    .A(deslocador_1_a_prime_b_prime[10]), .B(B[10]), .C0(OpCode[4]), .C1(OpCode[3]), .C2(OpCode[2]),
    .C3(OpCode[1]), .C4(OpCode[0]));
  ALUcell _18 (
    .Vem1(_17_vai1), .Bin(_17_bout), .S(S[18]), .Vai1(_18_vai1), .Bout(_18_bout),
    .A(deslocador_1_a_prime_b_prime[18]), .B(B[18]), .C0(OpCode[4]), .C1(OpCode[3]), .C2(OpCode[2]),
    .C3(OpCode[1]), .C4(OpCode[0]));
  ALUcell _26 (
    .Vem1(_25_vai1), .Bin(_25_bout), .S(S[26]), .Vai1(_26_vai1), .Bout(_26_bout),
    .A(deslocador_1_a_prime_b_prime[26]), .B(B[26]), .C0(OpCode[4]), .C1(OpCode[3]), .C2(OpCode[2]),
    .C3(OpCode[1]), .C4(OpCode[0]));
  ALUcell _3 (
    .Vem1(_2_vai1), .Bin(_2_bout), .S(S[3]), .Vai1(_3_vai1), .Bout(_3_bout),
    .A(deslocador_1_a_prime_b_prime[3]), .B(B[3]), .C0(OpCode[4]), .C1(OpCode[3]), .C2(OpCode[2]),
    .C3(OpCode[1]), .C4(OpCode[0]));
  ALUcell _11 (
    .Vem1(_10_vai1), .Bin(_10_bout), .S(S[11]), .Vai1(_11_vai1), .Bout(_11_bout),
    .A(deslocador_1_a_prime_b_prime[11]), .B(B[11]), .C0(OpCode[4]), .C1(OpCode[3]), .C2(OpCode[2]),
    .C3(OpCode[1]), .C4(OpCode[0]));
  ALUcell _19 (
    .Vem1(_18_vai1), .Bin(_18_bout), .S(S[19]), .Vai1(_19_vai1), .Bout(_19_bout),
    .A(deslocador_1_a_prime_b_prime[19]), .B(B[19]), .C0(OpCode[4]), .C1(OpCode[3]), .C2(OpCode[2]),
    .C3(OpCode[1]), .C4(OpCode[0]));
  ALUcell _27 (
    .Vem1(_26_vai1), .Bin(_26_bout), .S(S[27]), .Vai1(_27_vai1), .Bout(_27_bout),
    .A(deslocador_1_a_prime_b_prime[27]), .B(B[27]), .C0(OpCode[4]), .C1(OpCode[3]), .C2(OpCode[2]),
    .C3(OpCode[1]), .C4(OpCode[0]));
  ALUcell _4 (
    .Vem1(_3_vai1), .Bin(_3_bout), .S(S[4]), .Vai1(_4_vai1), .Bout(_4_bout),
    .A(deslocador_1_a_prime_b_prime[4]), .B(B[4]), .C0(OpCode[4]), .C1(OpCode[3]), .C2(OpCode[2]),
    .C3(OpCode[1]), .C4(OpCode[0]));
  ALUcell _12 (
    .Vem1(_11_vai1), .Bin(_11_bout), .S(S[12]), .Vai1(_12_vai1), .Bout(_12_bout),
    .A(deslocador_1_a_prime_b_prime[12]), .B(B[12]), .C0(OpCode[4]), .C1(OpCode[3]), .C2(OpCode[2]),
    .C3(OpCode[1]), .C4(OpCode[0]));
  ALUcell _20 (
    .Vem1(_19_vai1), .Bin(_19_bout), .S(S[20]), .Vai1(_20_vai1), .Bout(_20_bout),
    .A(deslocador_1_a_prime_b_prime[20]), .B(B[20]), .C0(OpCode[4]), .C1(OpCode[3]), .C2(OpCode[2]),
    .C3(OpCode[1]), .C4(OpCode[0]));
  ALUcell _28 (
    .Vem1(_27_vai1), .Bin(_27_bout), .S(S[28]), .Vai1(_28_vai1), .Bout(_28_bout),
    .A(deslocador_1_a_prime_b_prime[28]), .B(B[28]), .C0(OpCode[4]), .C1(OpCode[3]), .C2(OpCode[2]),
    .C3(OpCode[1]), .C4(OpCode[0]));
  ALUcell _5 (
    .Vem1(_4_vai1), .Bin(_4_bout), .S(S[5]), .Vai1(_5_vai1), .Bout(_5_bout),
    .A(deslocador_1_a_prime_b_prime[5]), .B(B[5]), .C0(OpCode[4]), .C1(OpCode[3]), .C2(OpCode[2]),
    .C3(OpCode[1]), .C4(OpCode[0]));
  ALUcell _13 (
    .Vem1(_12_vai1), .Bin(_12_bout), .S(S[13]), .Vai1(_13_vai1), .Bout(_13_bout),
    .A(deslocador_1_a_prime_b_prime[13]), .B(B[13]), .C0(OpCode[4]), .C1(OpCode[3]), .C2(OpCode[2]),
    .C3(OpCode[1]), .C4(OpCode[0]));
  ALUcell _21 (
    .Vem1(_20_vai1), .Bin(_20_bout), .S(S[21]), .Vai1(_21_vai1), .Bout(_21_bout),
    .A(deslocador_1_a_prime_b_prime[21]), .B(B[21]), .C0(OpCode[4]), .C1(OpCode[3]), .C2(OpCode[2]),
    .C3(OpCode[1]), .C4(OpCode[0]));
  ALUcell _29 (
    .Vem1(_28_vai1), .Bin(_28_bout), .S(S[29]), .Vai1(_29_vai1), .Bout(_29_bout),
    .A(deslocador_1_a_prime_b_prime[29]), .B(B[29]), .C0(OpCode[4]), .C1(OpCode[3]), .C2(OpCode[2]),
    .C3(OpCode[1]), .C4(OpCode[0]));
  ALUcell _6 (
    .Vem1(_5_vai1), .Bin(_5_bout), .S(S[6]), .Vai1(_6_vai1), .Bout(_6_bout),
    .A(deslocador_1_a_prime_b_prime[6]), .B(B[6]), .C0(OpCode[4]), .C1(OpCode[3]), .C2(OpCode[2]),
    .C3(OpCode[1]), .C4(OpCode[0]));
  ALUcell _14 (
    .Vem1(_13_vai1), .Bin(_13_bout), .S(S[14]), .Vai1(_14_vai1), .Bout(_14_bout),
    .A(deslocador_1_a_prime_b_prime[14]), .B(B[14]), .C0(OpCode[4]), .C1(OpCode[3]), .C2(OpCode[2]),
    .C3(OpCode[1]), .C4(OpCode[0]));
  ALUcell _22 (
    .Vem1(_21_vai1), .Bin(_21_bout), .S(S[22]), .Vai1(_22_vai1), .Bout(_22_bout),
    .A(deslocador_1_a_prime_b_prime[22]), .B(B[22]), .C0(OpCode[4]), .C1(OpCode[3]), .C2(OpCode[2]),
    .C3(OpCode[1]), .C4(OpCode[0]));
  ALUcell _30 (
    .Vem1(_29_vai1), .Bin(_29_bout), .S(S[30]), .Vai1(_30_vai1), .Bout(_30_bout),
    .A(deslocador_1_a_prime_b_prime[30]), .B(B[30]), .C0(OpCode[4]), .C1(OpCode[3]), .C2(OpCode[2]),
    .C3(OpCode[1]), .C4(OpCode[0]));
  ALUcell _7 (
    .Vem1(_6_vai1), .Bin(_6_bout), .S(S[7]), .Vai1(_7_vai1), .Bout(_7_bout),
    .A(deslocador_1_a_prime_b_prime[7]), .B(B[7]), .C0(OpCode[4]), .C1(OpCode[3]), .C2(OpCode[2]),
    .C3(OpCode[1]), .C4(OpCode[0]));
  ALUcell _15 (
    .Vem1(_14_vai1), .Bin(_14_bout), .S(S[15]), .Vai1(_15_vai1), .Bout(_15_bout),
    .A(deslocador_1_a_prime_b_prime[15]), .B(B[15]), .C0(OpCode[4]), .C1(OpCode[3]), .C2(OpCode[2]),
    .C3(OpCode[1]), .C4(OpCode[0]));
  ALUcell _23 (
    .Vem1(_22_vai1), .Bin(_22_bout), .S(S[23]), .Vai1(_23_vai1), .Bout(_23_bout),
    .A(deslocador_1_a_prime_b_prime[23]), .B(B[23]), .C0(OpCode[4]), .C1(OpCode[3]), .C2(OpCode[2]),
    .C3(OpCode[1]), .C4(OpCode[0]));
  ALUcell _31 (
    .Vem1(_30_vai1), .Bin(_30_bout), .S(S[31]), .Vai1(_31_vai1), .Bout(_31_bout),
    .A(deslocador_1_a_prime_b_prime[31]), .B(B[31]), .C0(OpCode[4]), .C1(OpCode[3]), .C2(OpCode[2]),
    .C3(OpCode[1]), .C4(OpCode[0]));
  and and_1 (and_1_out, ~deslocador_1_a_prime_b_prime[31], ~B[31], S[31]);  // AND_Gate
  and and_2 (and_2_out, deslocador_1_a_prime_b_prime[31], B[31], ~S[31]);  // AND_Gate
  and and_3 (and_3_out, OpCode[0], OpCode[1], ~OpCode[2], ~OpCode[3], ~OpCode[4]);  // AND_Gate
  and and_4 (and_4_out, ~OpCode[0], ~OpCode[1], OpCode[2], ~OpCode[3], ~OpCode[4]);  // AND_Gate
  or or_1 (or_1_out, and_1_out, and_2_out);
  or or_2 (or_2_out, and_3_out, and_4_out);
  Mux2 mux2_1 (.A(_31_vai1), .B(or_1_out), .Sel1(or_2_out), .S(out_9));
  nor nor_1 (out_7, S[0], S[1], S[2], S[3], S[4], S[5], S[6], S[7], S[8], S[9], S[10], S[11], S[12], S[13], S[14], S[15], S[16], S[17], S[18], S[19], S[20], S[21], S[22], S[23], S[24], S[25], S[26], S[27], S[28], S[29], S[30], S[31]);
  // also tied to GND on the sheet: _31_bout
endmodule

module Processador_teste (
  input  in_1,
  input  [31:0] in_2,
  input  [4:0] in_3,
  input  [31:0] in_4,
  input  [4:0] in_5,
  input  [4:0] in_6,
  input  [4:0] in_7,
  input  in_8,
  input  in_9,
  output out_10,
  output [31:0] out_11,
  output out_12
);

  wire [31:0] registradorr_1_datareg_a, registradorr_2_datareg_a;

  Registradorr registradorr_1 (
    .RegWR(in_3), .RegDATA_A(in_3), .WR(in_1), .RegIN(in_2), .DATAReg_A(registradorr_1_datareg_a));  // open: DataINRelay
  Registradorr registradorr_2 (
    .RegWR(in_5), .RegDATA_A(in_5), .WR(in_1), .RegIN(in_4), .DATAReg_A(registradorr_2_datareg_a));  // open: DataINRelay
  Processador processador_1 (
    .A(registradorr_1_datareg_a), .B(registradorr_2_datareg_a), .S(out_11), .Bin(in_9), .out_7(out_10),
    .out_9(out_12), .OpCode(in_6), .Shift_Amount(in_7), .L_R(in_8));
endmodule

module MUX2___32 (
  input  [31:0] in_1,
  input  [31:0] in_2,
  input  in_3,
  output [31:0] out_4
);

  Mux2 mux2_1 (.A(in_1[0]), .B(in_2[0]), .Sel1(in_3), .S(out_4[0]));
  Mux2 mux2_2 (.A(in_1[1]), .B(in_2[1]), .Sel1(in_3), .S(out_4[1]));
  Mux2 mux2_3 (.A(in_1[2]), .B(in_2[2]), .Sel1(in_3), .S(out_4[2]));
  Mux2 mux2_4 (.A(in_1[3]), .B(in_2[3]), .Sel1(in_3), .S(out_4[3]));
  Mux2 mux2_5 (.A(in_1[4]), .B(in_2[4]), .Sel1(in_3), .S(out_4[4]));
  Mux2 mux2_6 (.A(in_1[5]), .B(in_2[5]), .Sel1(in_3), .S(out_4[5]));
  Mux2 mux2_7 (.A(in_1[6]), .B(in_2[6]), .Sel1(in_3), .S(out_4[6]));
  Mux2 mux2_8 (.A(in_1[7]), .B(in_2[7]), .Sel1(in_3), .S(out_4[7]));
  Mux2 mux2_9 (.A(in_1[8]), .B(in_2[8]), .Sel1(in_3), .S(out_4[8]));
  Mux2 mux2_10 (.A(in_1[9]), .B(in_2[9]), .Sel1(in_3), .S(out_4[9]));
  Mux2 mux2_11 (.A(in_1[10]), .B(in_2[10]), .Sel1(in_3), .S(out_4[10]));
  Mux2 mux2_12 (.A(in_1[11]), .B(in_2[11]), .Sel1(in_3), .S(out_4[11]));
  Mux2 mux2_13 (.A(in_1[12]), .B(in_2[12]), .Sel1(in_3), .S(out_4[12]));
  Mux2 mux2_14 (.A(in_1[13]), .B(in_2[13]), .Sel1(in_3), .S(out_4[13]));
  Mux2 mux2_15 (.A(in_1[14]), .B(in_2[14]), .Sel1(in_3), .S(out_4[14]));
  Mux2 mux2_16 (.A(in_1[15]), .B(in_2[15]), .Sel1(in_3), .S(out_4[15]));
  Mux2 mux2_17 (.A(in_1[16]), .B(in_2[16]), .Sel1(in_3), .S(out_4[16]));
  Mux2 mux2_18 (.A(in_1[17]), .B(in_2[17]), .Sel1(in_3), .S(out_4[17]));
  Mux2 mux2_19 (.A(in_1[18]), .B(in_2[18]), .Sel1(in_3), .S(out_4[18]));
  Mux2 mux2_20 (.A(in_1[19]), .B(in_2[19]), .Sel1(in_3), .S(out_4[19]));
  Mux2 mux2_21 (.A(in_1[20]), .B(in_2[20]), .Sel1(in_3), .S(out_4[20]));
  Mux2 mux2_22 (.A(in_1[21]), .B(in_2[21]), .Sel1(in_3), .S(out_4[21]));
  Mux2 mux2_23 (.A(in_1[22]), .B(in_2[22]), .Sel1(in_3), .S(out_4[22]));
  Mux2 mux2_24 (.A(in_1[23]), .B(in_2[23]), .Sel1(in_3), .S(out_4[23]));
  Mux2 mux2_25 (.A(in_1[24]), .B(in_2[24]), .Sel1(in_3), .S(out_4[24]));
  Mux2 mux2_26 (.A(in_1[25]), .B(in_2[25]), .Sel1(in_3), .S(out_4[25]));
  Mux2 mux2_27 (.A(in_1[26]), .B(in_2[26]), .Sel1(in_3), .S(out_4[26]));
  Mux2 mux2_28 (.A(in_1[27]), .B(in_2[27]), .Sel1(in_3), .S(out_4[27]));
  Mux2 mux2_29 (.A(in_1[28]), .B(in_2[28]), .Sel1(in_3), .S(out_4[28]));
  Mux2 mux2_30 (.A(in_1[29]), .B(in_2[29]), .Sel1(in_3), .S(out_4[29]));
  Mux2 mux2_31 (.A(in_1[30]), .B(in_2[30]), .Sel1(in_3), .S(out_4[30]));
  Mux2 mux2_32 (.A(in_1[31]), .B(in_2[31]), .Sel1(in_3), .S(out_4[31]));
endmodule

module MUX16___4 (
  input  [15:0] in_1,
  input  in_2,
  input  in_3,
  output [3:0] out_4
);

  Mux4 mux4_1 (.A(in_1[0]), .B(in_1[1]), .C(in_1[2]), .D(in_1[3]), .in_5(in_2), .in_6(in_3), .S(out_4[0]));
  Mux4 mux4_2 (.A(in_1[4]), .B(in_1[5]), .C(in_1[6]), .D(in_1[7]), .in_5(in_2), .in_6(in_3), .S(out_4[1]));
  Mux4 mux4_3 (.A(in_1[8]), .B(in_1[9]), .C(in_1[10]), .D(in_1[11]), .in_5(in_2), .in_6(in_3), .S(out_4[2]));
  Mux4 mux4_4 (.A(in_1[12]), .B(in_1[13]), .C(in_1[14]), .D(in_1[15]), .in_5(in_2), .in_6(in_3), .S(out_4[3]));
endmodule

// L Shifter
module Left_Shifter (
  input  C0,
  input  C1,
  input  C2,
  input  C3,
  input  C4,
  input  [31:0] in_6,
  output [31:0] out_7
);

  Mux32_com_Mux16 _0 (
    .E0(in_6[0]), .E16(1'b0), .E1(1'b0), .E17(1'b0), .E2(1'b0), .E18(1'b0), .E3(1'b0), .E19(1'b0), .E4(1'b0),
    .E20(1'b0), .E5(1'b0), .E21(1'b0), .E6(1'b0), .E22(1'b0), .E7(1'b0), .E23(1'b0), .E8(1'b0), .E24(1'b0),
    .E9(1'b0), .E25(1'b0), .E10(1'b0), .E26(1'b0), .E11(1'b0), .E27(1'b0), .E12(1'b0), .E28(1'b0),
    .E13(1'b0), .E29(1'b0), .E14(1'b0), .E30(1'b0), .E15(1'b0), .E31(1'b0), .in_37(C0), .in_33(C1),
    .in_34(C2), .in_35(C3), .S(out_7[0]), .in_36(C4));
  Mux32_com_Mux16 _8 (
    .E0(in_6[8]), .E16(1'b0), .E1(in_6[7]), .E17(1'b0), .E2(in_6[6]), .E18(1'b0), .E3(in_6[5]), .E19(1'b0),
    .E4(in_6[4]), .E20(1'b0), .E5(in_6[3]), .E21(1'b0), .E6(in_6[2]), .E22(1'b0), .E7(in_6[1]), .E23(1'b0),
    .E8(in_6[0]), .E24(1'b0), .E9(1'b0), .E25(1'b0), .E10(1'b0), .E26(1'b0), .E11(1'b0), .E27(1'b0),
    .E12(1'b0), .E28(1'b0), .E13(1'b0), .E29(1'b0), .E14(1'b0), .E30(1'b0), .E15(1'b0), .E31(1'b0),
    .in_37(C0), .in_33(C1), .in_34(C2), .in_35(C3), .S(out_7[8]), .in_36(C4));
  Mux32_com_Mux16 _16 (
    .E0(in_6[16]), .E16(in_6[0]), .E1(in_6[15]), .E17(1'b0), .E2(in_6[14]), .E18(1'b0), .E3(in_6[13]),
    .E19(1'b0), .E4(in_6[12]), .E20(1'b0), .E5(in_6[11]), .E21(1'b0), .E6(in_6[10]), .E22(1'b0),
    .E7(in_6[9]), .E23(1'b0), .E8(in_6[8]), .E24(1'b0), .E9(in_6[7]), .E25(1'b0), .E10(in_6[6]), .E26(1'b0),
    .E11(in_6[5]), .E27(1'b0), .E12(in_6[4]), .E28(1'b0), .E13(in_6[3]), .E29(1'b0), .E14(in_6[2]),
    .E30(1'b0), .E15(in_6[1]), .E31(1'b0), .in_37(C0), .in_33(C1), .in_34(C2), .in_35(C3), .S(out_7[16]),
    .in_36(C4));
  Mux32_com_Mux16 _24 (
    .E0(in_6[24]), .E16(in_6[8]), .E1(in_6[23]), .E17(in_6[7]), .E2(in_6[22]), .E18(in_6[6]), .E3(in_6[21]),
    .E19(in_6[5]), .E4(in_6[20]), .E20(in_6[4]), .E5(in_6[19]), .E21(in_6[3]), .E6(in_6[18]), .E22(in_6[2]),
    .E7(in_6[17]), .E23(in_6[1]), .E8(in_6[16]), .E24(in_6[0]), .E9(in_6[15]), .E25(1'b0), .E10(in_6[14]),
    .E26(1'b0), .E11(in_6[13]), .E27(1'b0), .E12(in_6[12]), .E28(1'b0), .E13(in_6[11]), .E29(1'b0),
    .E14(in_6[10]), .E30(1'b0), .E15(in_6[9]), .E31(1'b0), .in_37(C0), .in_33(C1), .in_34(C2), .in_35(C3),
    .S(out_7[24]), .in_36(C4));
  Mux32_com_Mux16 _1 (
    .E0(in_6[1]), .E16(1'b0), .E1(in_6[0]), .E17(1'b0), .E2(1'b0), .E18(1'b0), .E3(1'b0), .E19(1'b0),
    .E4(1'b0), .E20(1'b0), .E5(1'b0), .E21(1'b0), .E6(1'b0), .E22(1'b0), .E7(1'b0), .E23(1'b0), .E8(1'b0),
    .E24(1'b0), .E9(1'b0), .E25(1'b0), .E10(1'b0), .E26(1'b0), .E11(1'b0), .E27(1'b0), .E12(1'b0),
    .E28(1'b0), .E13(1'b0), .E29(1'b0), .E14(1'b0), .E30(1'b0), .E15(1'b0), .E31(1'b0), .in_37(C0),
    .in_33(C1), .in_34(C2), .in_35(C3), .S(out_7[1]), .in_36(C4));
  Mux32_com_Mux16 _9 (
    .E0(in_6[9]), .E16(1'b0), .E1(in_6[8]), .E17(1'b0), .E2(in_6[7]), .E18(1'b0), .E3(in_6[6]), .E19(1'b0),
    .E4(in_6[5]), .E20(1'b0), .E5(in_6[4]), .E21(1'b0), .E6(in_6[3]), .E22(1'b0), .E7(in_6[2]), .E23(1'b0),
    .E8(in_6[1]), .E24(1'b0), .E9(in_6[0]), .E25(1'b0), .E10(1'b0), .E26(1'b0), .E11(1'b0), .E27(1'b0),
    .E12(1'b0), .E28(1'b0), .E13(1'b0), .E29(1'b0), .E14(1'b0), .E30(1'b0), .E15(1'b0), .E31(1'b0),
    .in_37(C0), .in_33(C1), .in_34(C2), .in_35(C3), .S(out_7[9]), .in_36(C4));
  Mux32_com_Mux16 _17 (
    .E0(in_6[17]), .E16(in_6[1]), .E1(in_6[16]), .E17(in_6[0]), .E2(in_6[15]), .E18(1'b0), .E3(in_6[14]),
    .E19(1'b0), .E4(in_6[13]), .E20(1'b0), .E5(in_6[12]), .E21(1'b0), .E6(in_6[11]), .E22(1'b0),
    .E7(in_6[10]), .E23(1'b0), .E8(in_6[9]), .E24(1'b0), .E9(in_6[8]), .E25(1'b0), .E10(in_6[7]), .E26(1'b0),
    .E11(in_6[6]), .E27(1'b0), .E12(in_6[5]), .E28(1'b0), .E13(in_6[4]), .E29(1'b0), .E14(in_6[3]),
    .E30(1'b0), .E15(in_6[2]), .E31(1'b0), .in_37(C0), .in_33(C1), .in_34(C2), .in_35(C3), .S(out_7[17]),
    .in_36(C4));
  Mux32_com_Mux16 _25 (
    .E0(in_6[25]), .E16(in_6[9]), .E1(in_6[24]), .E17(in_6[8]), .E2(in_6[23]), .E18(in_6[7]), .E3(in_6[22]),
    .E19(in_6[6]), .E4(in_6[21]), .E20(in_6[5]), .E5(in_6[20]), .E21(in_6[4]), .E6(in_6[19]), .E22(in_6[3]),
    .E7(in_6[18]), .E23(in_6[2]), .E8(in_6[17]), .E24(in_6[1]), .E9(in_6[16]), .E25(in_6[0]), .E10(in_6[15]),
    .E11(in_6[14]), .E27(1'b0), .E12(in_6[13]), .E28(1'b0), .E13(in_6[12]), .E29(1'b0), .E14(in_6[11]),
    .E30(1'b0), .E15(in_6[10]), .E31(1'b0), .in_37(C0), .in_33(C1), .in_34(C2), .in_35(C3), .S(out_7[25]),
    .in_36(C4));  // open: E26
  Mux32_com_Mux16 _2 (
    .E0(in_6[2]), .E16(1'b0), .E1(in_6[1]), .E17(1'b0), .E2(in_6[0]), .E18(1'b0), .E3(1'b0), .E19(1'b0),
    .E4(1'b0), .E20(1'b0), .E5(1'b0), .E21(1'b0), .E6(1'b0), .E22(1'b0), .E7(1'b0), .E23(1'b0), .E8(1'b0),
    .E24(1'b0), .E9(1'b0), .E25(1'b0), .E10(1'b0), .E26(1'b0), .E11(1'b0), .E27(1'b0), .E12(1'b0),
    .E28(1'b0), .E13(1'b0), .E29(1'b0), .E14(1'b0), .E30(1'b0), .E15(1'b0), .E31(1'b0), .in_37(C0),
    .in_33(C1), .in_34(C2), .in_35(C3), .S(out_7[2]), .in_36(C4));
  Mux32_com_Mux16 _10 (
    .E0(in_6[10]), .E16(1'b0), .E1(in_6[9]), .E17(1'b0), .E2(in_6[8]), .E18(1'b0), .E3(in_6[7]), .E19(1'b0),
    .E4(in_6[6]), .E20(1'b0), .E5(in_6[5]), .E21(1'b0), .E6(in_6[4]), .E22(1'b0), .E7(in_6[3]), .E23(1'b0),
    .E8(in_6[2]), .E24(1'b0), .E9(in_6[1]), .E25(1'b0), .E10(in_6[0]), .E26(1'b0), .E11(1'b0), .E27(1'b0),
    .E12(1'b0), .E28(1'b0), .E13(1'b0), .E29(1'b0), .E14(1'b0), .E30(1'b0), .E15(1'b0), .E31(1'b0),
    .in_37(C0), .in_33(C1), .in_34(C2), .in_35(C3), .S(out_7[10]), .in_36(C4));
  Mux32_com_Mux16 _18 (
    .E0(in_6[18]), .E16(in_6[2]), .E1(in_6[17]), .E17(in_6[1]), .E2(in_6[16]), .E18(in_6[0]), .E3(in_6[15]),
    .E19(1'b0), .E4(in_6[14]), .E20(1'b0), .E5(in_6[13]), .E21(1'b0), .E6(in_6[12]), .E22(1'b0),
    .E7(in_6[11]), .E23(1'b0), .E8(in_6[10]), .E24(1'b0), .E9(in_6[9]), .E25(1'b0), .E10(in_6[8]),
    .E26(1'b0), .E11(in_6[7]), .E27(1'b0), .E12(in_6[6]), .E28(1'b0), .E13(in_6[5]), .E29(1'b0),
    .E14(in_6[4]), .E30(1'b0), .E15(in_6[3]), .E31(1'b0), .in_37(C0), .in_33(C1), .in_34(C2), .in_35(C3),
    .S(out_7[18]), .in_36(C4));
  Mux32_com_Mux16 _26 (
    .E0(in_6[26]), .E16(in_6[10]), .E1(in_6[25]), .E17(in_6[9]), .E2(in_6[24]), .E18(in_6[8]), .E3(in_6[23]),
    .E19(in_6[7]), .E4(in_6[22]), .E20(in_6[6]), .E5(in_6[21]), .E21(in_6[5]), .E6(in_6[20]), .E22(in_6[4]),
    .E7(in_6[19]), .E23(in_6[3]), .E8(in_6[18]), .E24(in_6[2]), .E9(in_6[17]), .E25(in_6[1]), .E10(in_6[16]),
    .E26(in_6[0]), .E11(in_6[15]), .E27(1'b0), .E12(in_6[14]), .E28(1'b0), .E13(in_6[13]), .E29(1'b0),
    .E14(in_6[12]), .E30(1'b0), .E15(in_6[11]), .E31(1'b0), .in_37(C0), .in_33(C1), .in_34(C2), .in_35(C3),
    .S(out_7[26]), .in_36(C4));
  Mux32_com_Mux16 _3 (
    .E0(in_6[3]), .E16(1'b0), .E1(in_6[2]), .E17(1'b0), .E2(in_6[1]), .E18(1'b0), .E3(in_6[0]), .E19(1'b0),
    .E4(1'b0), .E20(1'b0), .E5(1'b0), .E21(1'b0), .E6(1'b0), .E22(1'b0), .E7(1'b0), .E23(1'b0), .E8(1'b0),
    .E24(1'b0), .E9(1'b0), .E25(1'b0), .E10(1'b0), .E26(1'b0), .E11(1'b0), .E27(1'b0), .E12(1'b0),
    .E28(1'b0), .E13(1'b0), .E29(1'b0), .E14(1'b0), .E30(1'b0), .E15(1'b0), .E31(1'b0), .in_37(C0),
    .in_33(C1), .in_34(C2), .in_35(C3), .S(out_7[3]), .in_36(C4));
  Mux32_com_Mux16 _11 (
    .E0(in_6[11]), .E16(1'b0), .E1(in_6[10]), .E17(1'b0), .E2(in_6[9]), .E18(1'b0), .E3(in_6[8]), .E19(1'b0),
    .E4(in_6[7]), .E20(1'b0), .E5(in_6[6]), .E21(1'b0), .E6(in_6[5]), .E22(1'b0), .E7(in_6[4]), .E23(1'b0),
    .E8(in_6[3]), .E24(1'b0), .E9(in_6[2]), .E25(1'b0), .E10(in_6[1]), .E26(1'b0), .E11(in_6[0]), .E27(1'b0),
    .E12(1'b0), .E28(1'b0), .E13(1'b0), .E29(1'b0), .E14(1'b0), .E30(1'b0), .E15(1'b0), .E31(1'b0),
    .in_37(C0), .in_33(C1), .in_34(C2), .in_35(C3), .S(out_7[11]), .in_36(C4));
  Mux32_com_Mux16 _19 (
    .E0(in_6[19]), .E16(in_6[3]), .E1(in_6[18]), .E17(in_6[2]), .E2(in_6[17]), .E18(in_6[1]), .E3(in_6[16]),
    .E19(in_6[0]), .E4(in_6[15]), .E20(1'b0), .E5(in_6[14]), .E21(1'b0), .E6(in_6[13]), .E22(1'b0),
    .E7(in_6[12]), .E23(1'b0), .E8(in_6[11]), .E24(1'b0), .E9(in_6[10]), .E25(1'b0), .E10(in_6[9]),
    .E26(1'b0), .E11(in_6[8]), .E27(1'b0), .E12(in_6[7]), .E28(1'b0), .E13(in_6[6]), .E29(1'b0),
    .E14(in_6[5]), .E30(1'b0), .E15(in_6[4]), .E31(1'b0), .in_37(C0), .in_33(C1), .in_34(C2), .in_35(C3),
    .S(out_7[19]), .in_36(C4));
  Mux32_com_Mux16 _27 (
    .E0(in_6[27]), .E16(in_6[11]), .E1(in_6[26]), .E17(in_6[10]), .E2(in_6[25]), .E18(in_6[9]),
    .E3(in_6[24]), .E19(in_6[8]), .E4(in_6[23]), .E20(in_6[7]), .E5(in_6[22]), .E21(in_6[6]), .E6(in_6[21]),
    .E22(in_6[5]), .E7(in_6[20]), .E23(in_6[4]), .E8(in_6[19]), .E24(in_6[3]), .E9(in_6[18]), .E25(in_6[2]),
    .E10(in_6[17]), .E26(in_6[1]), .E11(in_6[16]), .E27(in_6[0]), .E12(in_6[15]), .E28(1'b0), .E13(in_6[14]),
    .E29(1'b0), .E14(in_6[13]), .E30(1'b0), .E15(in_6[12]), .E31(1'b0), .in_37(C0), .in_33(C1), .in_34(C2),
    .in_35(C3), .S(out_7[27]), .in_36(C4));
  Mux32_com_Mux16 _4 (
    .E0(in_6[4]), .E16(1'b0), .E1(in_6[3]), .E17(1'b0), .E2(in_6[2]), .E18(1'b0), .E3(in_6[1]), .E19(1'b0),
    .E4(in_6[0]), .E20(1'b0), .E5(1'b0), .E21(1'b0), .E6(1'b0), .E22(1'b0), .E7(1'b0), .E23(1'b0), .E8(1'b0),
    .E24(1'b0), .E9(1'b0), .E25(1'b0), .E10(1'b0), .E26(1'b0), .E11(1'b0), .E27(1'b0), .E12(1'b0),
    .E28(1'b0), .E13(1'b0), .E29(1'b0), .E14(1'b0), .E30(1'b0), .E15(1'b0), .E31(1'b0), .in_37(C0),
    .in_33(C1), .in_34(C2), .in_35(C3), .S(out_7[4]), .in_36(C4));
  Mux32_com_Mux16 _12 (
    .E0(in_6[12]), .E16(1'b0), .E1(in_6[11]), .E17(1'b0), .E2(in_6[10]), .E18(1'b0), .E3(in_6[9]),
    .E19(1'b0), .E4(in_6[8]), .E20(1'b0), .E5(in_6[7]), .E21(1'b0), .E6(in_6[6]), .E22(1'b0), .E7(in_6[5]),
    .E23(1'b0), .E8(in_6[4]), .E24(1'b0), .E9(in_6[3]), .E25(1'b0), .E10(in_6[2]), .E26(1'b0), .E11(in_6[1]),
    .E27(1'b0), .E12(in_6[0]), .E28(1'b0), .E13(1'b0), .E29(1'b0), .E14(1'b0), .E30(1'b0), .E15(1'b0),
    .E31(1'b0), .in_37(C0), .in_33(C1), .in_34(C2), .in_35(C3), .S(out_7[12]), .in_36(C4));
  Mux32_com_Mux16 _20 (
    .E0(in_6[20]), .E16(in_6[4]), .E1(in_6[19]), .E17(in_6[3]), .E2(in_6[18]), .E18(in_6[2]), .E3(in_6[17]),
    .E19(in_6[1]), .E4(in_6[16]), .E20(in_6[0]), .E5(in_6[15]), .E21(1'b0), .E6(in_6[14]), .E22(1'b0),
    .E7(in_6[13]), .E23(1'b0), .E8(in_6[12]), .E24(1'b0), .E9(in_6[11]), .E25(1'b0), .E10(in_6[10]),
    .E26(1'b0), .E11(in_6[9]), .E27(1'b0), .E12(in_6[8]), .E28(1'b0), .E13(in_6[7]), .E29(1'b0),
    .E14(in_6[6]), .E30(1'b0), .E15(in_6[5]), .E31(1'b0), .in_37(C0), .in_33(C1), .in_34(C2), .in_35(C3),
    .S(out_7[20]), .in_36(C4));
  Mux32_com_Mux16 _28 (
    .E0(in_6[28]), .E16(in_6[12]), .E1(in_6[27]), .E17(in_6[11]), .E2(in_6[26]), .E18(in_6[10]),
    .E3(in_6[25]), .E19(in_6[9]), .E4(in_6[24]), .E20(in_6[8]), .E5(in_6[23]), .E21(in_6[7]), .E6(in_6[22]),
    .E22(in_6[6]), .E7(in_6[21]), .E23(in_6[5]), .E8(in_6[20]), .E24(in_6[4]), .E9(in_6[19]), .E25(in_6[3]),
    .E10(in_6[18]), .E26(in_6[2]), .E11(in_6[17]), .E27(in_6[1]), .E12(in_6[16]), .E28(in_6[0]),
    .E13(in_6[15]), .E29(1'b0), .E14(in_6[14]), .E30(1'b0), .E15(in_6[13]), .E31(1'b0), .in_37(C0),
    .in_33(C1), .in_34(C2), .in_35(C3), .S(out_7[28]), .in_36(C4));
  Mux32_com_Mux16 _5 (
    .E0(in_6[5]), .E16(1'b0), .E1(in_6[4]), .E17(1'b0), .E2(in_6[3]), .E18(1'b0), .E3(in_6[2]), .E19(1'b0),
    .E4(in_6[1]), .E20(1'b0), .E5(in_6[0]), .E21(1'b0), .E6(1'b0), .E22(1'b0), .E7(1'b0), .E23(1'b0),
    .E8(1'b0), .E24(1'b0), .E9(1'b0), .E25(1'b0), .E10(1'b0), .E26(1'b0), .E11(1'b0), .E27(1'b0), .E12(1'b0),
    .E28(1'b0), .E13(1'b0), .E29(1'b0), .E14(1'b0), .E30(1'b0), .E15(1'b0), .E31(1'b0), .in_37(C0),
    .in_33(C1), .in_34(C2), .in_35(C3), .S(out_7[5]), .in_36(C4));
  Mux32_com_Mux16 _13 (
    .E0(in_6[13]), .E16(1'b0), .E1(in_6[12]), .E17(1'b0), .E2(in_6[11]), .E18(1'b0), .E3(in_6[10]),
    .E19(1'b0), .E4(in_6[9]), .E20(1'b0), .E5(in_6[8]), .E21(1'b0), .E6(in_6[7]), .E22(1'b0), .E7(in_6[6]),
    .E23(1'b0), .E8(in_6[5]), .E24(1'b0), .E9(in_6[4]), .E25(1'b0), .E10(in_6[3]), .E26(1'b0), .E11(in_6[2]),
    .E27(1'b0), .E12(in_6[1]), .E28(1'b0), .E13(in_6[0]), .E29(1'b0), .E14(1'b0), .E30(1'b0), .E15(1'b0),
    .E31(1'b0), .in_37(C0), .in_33(C1), .in_34(C2), .in_35(C3), .S(out_7[13]), .in_36(C4));
  Mux32_com_Mux16 _21 (
    .E0(in_6[21]), .E16(in_6[5]), .E1(in_6[20]), .E17(in_6[4]), .E2(in_6[19]), .E18(in_6[3]), .E3(in_6[18]),
    .E19(in_6[2]), .E4(in_6[17]), .E20(in_6[1]), .E5(in_6[16]), .E21(in_6[0]), .E6(in_6[15]), .E22(1'b0),
    .E7(in_6[14]), .E23(1'b0), .E8(in_6[13]), .E24(1'b0), .E9(in_6[12]), .E25(1'b0), .E10(in_6[11]),
    .E26(1'b0), .E11(in_6[10]), .E27(1'b0), .E12(in_6[9]), .E28(1'b0), .E13(in_6[8]), .E29(1'b0),
    .E14(in_6[7]), .E30(1'b0), .E15(in_6[6]), .E31(1'b0), .in_37(C0), .in_33(C1), .in_34(C2), .in_35(C3),
    .S(out_7[21]), .in_36(C4));
  Mux32_com_Mux16 _29 (
    .E0(in_6[29]), .E16(in_6[13]), .E1(in_6[28]), .E17(in_6[12]), .E2(in_6[27]), .E18(in_6[11]),
    .E3(in_6[26]), .E19(in_6[10]), .E4(in_6[25]), .E20(in_6[9]), .E5(in_6[24]), .E21(in_6[8]), .E6(in_6[23]),
    .E22(in_6[7]), .E7(in_6[22]), .E23(in_6[6]), .E8(in_6[21]), .E24(in_6[5]), .E9(in_6[20]), .E25(in_6[4]),
    .E10(in_6[19]), .E26(in_6[3]), .E11(in_6[18]), .E27(in_6[2]), .E12(in_6[17]), .E28(in_6[1]),
    .E13(in_6[16]), .E29(in_6[0]), .E14(in_6[15]), .E30(1'b0), .E15(in_6[14]), .E31(1'b0), .in_37(C0),
    .in_33(C1), .in_34(C2), .in_35(C3), .S(out_7[29]), .in_36(C4));
  Mux32_com_Mux16 _6 (
    .E0(in_6[6]), .E16(1'b0), .E1(in_6[5]), .E17(1'b0), .E2(in_6[4]), .E18(1'b0), .E3(in_6[3]), .E19(1'b0),
    .E4(in_6[2]), .E20(1'b0), .E5(in_6[1]), .E21(1'b0), .E6(in_6[0]), .E22(1'b0), .E7(1'b0), .E23(1'b0),
    .E8(1'b0), .E24(1'b0), .E9(1'b0), .E25(1'b0), .E10(1'b0), .E26(1'b0), .E11(1'b0), .E27(1'b0), .E12(1'b0),
    .E28(1'b0), .E13(1'b0), .E29(1'b0), .E14(1'b0), .E30(1'b0), .E15(1'b0), .E31(1'b0), .in_37(C0),
    .in_33(C1), .in_34(C2), .in_35(C3), .S(out_7[6]), .in_36(C4));
  Mux32_com_Mux16 _14 (
    .E0(in_6[14]), .E16(1'b0), .E1(in_6[13]), .E17(1'b0), .E2(in_6[12]), .E18(1'b0), .E3(in_6[11]),
    .E19(1'b0), .E4(in_6[10]), .E20(1'b0), .E5(in_6[9]), .E21(1'b0), .E6(in_6[8]), .E22(1'b0), .E7(in_6[7]),
    .E23(1'b0), .E8(in_6[6]), .E24(1'b0), .E9(in_6[5]), .E25(1'b0), .E10(in_6[4]), .E26(1'b0), .E11(in_6[3]),
    .E27(1'b0), .E12(in_6[2]), .E28(1'b0), .E13(in_6[1]), .E29(1'b0), .E14(in_6[0]), .E30(1'b0), .E15(1'b0),
    .E31(1'b0), .in_37(C0), .in_33(C1), .in_34(C2), .in_35(C3), .S(out_7[14]), .in_36(C4));
  Mux32_com_Mux16 _22 (
    .E0(in_6[22]), .E16(in_6[6]), .E1(in_6[21]), .E17(in_6[5]), .E2(in_6[20]), .E18(in_6[4]), .E3(in_6[19]),
    .E19(in_6[3]), .E4(in_6[18]), .E20(in_6[2]), .E5(in_6[17]), .E21(in_6[1]), .E6(in_6[16]), .E22(in_6[0]),
    .E7(in_6[15]), .E23(1'b0), .E8(in_6[14]), .E24(1'b0), .E9(in_6[13]), .E25(1'b0), .E10(in_6[12]),
    .E26(1'b0), .E11(in_6[11]), .E27(1'b0), .E12(in_6[10]), .E28(1'b0), .E13(in_6[9]), .E29(1'b0),
    .E14(in_6[8]), .E30(1'b0), .E15(in_6[7]), .E31(1'b0), .in_37(C0), .in_33(C1), .in_34(C2), .in_35(C3),
    .S(out_7[22]), .in_36(C4));
  Mux32_com_Mux16 _30 (
    .E0(in_6[30]), .E16(in_6[14]), .E1(in_6[29]), .E17(in_6[13]), .E2(in_6[28]), .E18(in_6[12]),
    .E3(in_6[27]), .E19(in_6[11]), .E4(in_6[26]), .E20(in_6[10]), .E5(in_6[25]), .E21(in_6[9]),
    .E6(in_6[24]), .E22(in_6[8]), .E7(in_6[23]), .E23(in_6[7]), .E8(in_6[22]), .E24(in_6[6]), .E9(in_6[21]),
    .E25(in_6[5]), .E10(in_6[20]), .E26(in_6[4]), .E11(in_6[19]), .E27(in_6[3]), .E12(in_6[18]),
    .E28(in_6[2]), .E13(in_6[17]), .E29(in_6[1]), .E14(in_6[16]), .E30(in_6[0]), .E15(in_6[15]), .E31(1'b0),
    .in_37(C0), .in_33(C1), .in_34(C2), .in_35(C3), .S(out_7[30]), .in_36(C4));
  Mux32_com_Mux16 _7 (
    .E0(in_6[7]), .E16(1'b0), .E1(in_6[6]), .E17(1'b0), .E2(in_6[5]), .E18(1'b0), .E3(in_6[4]), .E19(1'b0),
    .E4(in_6[3]), .E20(1'b0), .E5(in_6[2]), .E21(1'b0), .E6(in_6[1]), .E22(1'b0), .E7(in_6[0]), .E23(1'b0),
    .E8(1'b0), .E24(1'b0), .E9(1'b0), .E25(1'b0), .E10(1'b0), .E26(1'b0), .E11(1'b0), .E27(1'b0), .E12(1'b0),
    .E28(1'b0), .E13(1'b0), .E29(1'b0), .E14(1'b0), .E30(1'b0), .E15(1'b0), .E31(1'b0), .in_37(C0),
    .in_33(C1), .in_34(C2), .in_35(C3), .S(out_7[7]), .in_36(C4));
  Mux32_com_Mux16 _15 (
    .E0(in_6[15]), .E16(1'b0), .E1(in_6[14]), .E17(1'b0), .E2(in_6[13]), .E18(1'b0), .E3(in_6[12]),
    .E19(1'b0), .E4(in_6[11]), .E20(1'b0), .E5(in_6[10]), .E21(1'b0), .E6(in_6[9]), .E22(1'b0), .E7(in_6[8]),
    .E23(1'b0), .E8(in_6[7]), .E24(1'b0), .E9(in_6[6]), .E25(1'b0), .E10(in_6[5]), .E26(1'b0), .E11(in_6[4]),
    .E27(1'b0), .E12(in_6[3]), .E28(1'b0), .E13(in_6[2]), .E29(1'b0), .E14(in_6[1]), .E30(1'b0),
    .E15(in_6[0]), .E31(1'b0), .in_37(C0), .in_33(C1), .in_34(C2), .in_35(C3), .S(out_7[15]), .in_36(C4));
  Mux32_com_Mux16 _23 (
    .E0(in_6[23]), .E16(in_6[7]), .E1(in_6[22]), .E17(in_6[6]), .E2(in_6[21]), .E18(in_6[5]), .E3(in_6[20]),
    .E19(in_6[4]), .E4(in_6[19]), .E20(in_6[3]), .E5(in_6[18]), .E21(in_6[2]), .E6(in_6[17]), .E22(in_6[1]),
    .E7(in_6[16]), .E23(in_6[0]), .E8(in_6[15]), .E24(1'b0), .E9(in_6[14]), .E25(1'b0), .E10(in_6[13]),
    .E26(1'b0), .E11(in_6[12]), .E27(1'b0), .E12(in_6[11]), .E28(1'b0), .E13(in_6[10]), .E29(1'b0),
    .E14(in_6[9]), .E30(1'b0), .E15(in_6[8]), .E31(1'b0), .in_37(C0), .in_33(C1), .in_34(C2), .in_35(C3),
    .S(out_7[23]), .in_36(C4));
  Mux32_com_Mux16 _31 (
    .E0(in_6[31]), .E16(in_6[15]), .E1(in_6[30]), .E17(in_6[14]), .E2(in_6[29]), .E18(in_6[13]),
    .E3(in_6[28]), .E19(in_6[12]), .E4(in_6[27]), .E20(in_6[11]), .E5(in_6[26]), .E21(in_6[10]),
    .E6(in_6[25]), .E22(in_6[9]), .E7(in_6[24]), .E23(in_6[8]), .E8(in_6[23]), .E24(in_6[7]), .E9(in_6[22]),
    .E25(in_6[6]), .E10(in_6[21]), .E26(in_6[5]), .E11(in_6[20]), .E27(in_6[4]), .E12(in_6[19]),
    .E28(in_6[3]), .E13(in_6[18]), .E29(in_6[2]), .E14(in_6[17]), .E30(in_6[1]), .E15(in_6[16]),
    .E31(in_6[0]), .in_37(C0), .in_33(C1), .in_34(C2), .in_35(C3), .S(out_7[31]), .in_36(C4));
endmodule

// R Shifter
module Right_shifter (
  input  C0,
  input  C1,
  input  C2,
  input  C3,
  input  C4,
  input  [31:0] in_6,
  output [31:0] out_7
);

  Mux32_com_Mux16 _0 (
    .E0(in_6[0]), .E16(in_6[16]), .E1(in_6[1]), .E17(in_6[17]), .E2(in_6[2]), .E18(in_6[18]), .E3(in_6[3]),
    .E19(in_6[19]), .E4(in_6[4]), .E20(in_6[20]), .E5(in_6[5]), .E21(in_6[21]), .E6(in_6[6]), .E22(in_6[22]),
    .E7(in_6[7]), .E23(in_6[23]), .E8(in_6[8]), .E24(in_6[24]), .E9(in_6[9]), .E25(in_6[25]), .E10(in_6[10]),
    .E26(in_6[26]), .E11(in_6[11]), .E27(in_6[27]), .E12(in_6[12]), .E28(in_6[28]), .E13(in_6[13]),
    .E29(in_6[29]), .E14(in_6[14]), .E30(in_6[30]), .E15(in_6[15]), .E31(in_6[31]), .in_37(C0), .in_33(C1),
    .in_34(C2), .in_35(C3), .S(out_7[0]), .in_36(C4));
  Mux32_com_Mux16 _8 (
    .E0(in_6[8]), .E16(in_6[24]), .E1(in_6[9]), .E17(in_6[25]), .E2(in_6[10]), .E18(in_6[26]), .E3(in_6[11]),
    .E19(in_6[27]), .E4(in_6[12]), .E20(in_6[28]), .E5(in_6[13]), .E21(in_6[29]), .E6(in_6[14]),
    .E22(in_6[30]), .E7(in_6[15]), .E23(in_6[31]), .E8(in_6[16]), .E24(1'b0), .E9(in_6[17]), .E25(1'b0),
    .E10(in_6[18]), .E26(1'b0), .E11(in_6[19]), .E27(1'b0), .E12(in_6[20]), .E28(1'b0), .E13(in_6[21]),
    .E29(1'b0), .E14(in_6[22]), .E30(1'b0), .E15(in_6[23]), .E31(1'b0), .in_37(C0), .in_33(C1), .in_34(C2),
    .in_35(C3), .S(out_7[8]), .in_36(C4));
  Mux32_com_Mux16 _16 (
    .E0(in_6[16]), .E16(1'b0), .E1(in_6[17]), .E17(1'b0), .E2(in_6[18]), .E18(1'b0), .E3(in_6[19]),
    .E19(1'b0), .E4(in_6[21]), .E20(1'b0), .E5(in_6[22]), .E21(1'b0), .E6(in_6[23]), .E22(1'b0),
    .E7(in_6[24]), .E23(1'b0), .E8(in_6[25]), .E24(1'b0), .E9(in_6[26]), .E25(1'b0), .E10(in_6[27]),
    .E26(1'b0), .E11(in_6[28]), .E27(1'b0), .E12(in_6[29]), .E28(1'b0), .E13(in_6[30]), .E29(1'b0),
    .E14(in_6[31]), .E30(1'b0), .E15(1'b0), .E31(1'b0), .in_37(C0), .in_33(C1), .in_34(C2), .in_35(C3),
    .S(out_7[16]), .in_36(C4));
  Mux32_com_Mux16 _24 (
    .E0(in_6[24]), .E16(1'b0), .E1(in_6[25]), .E17(1'b0), .E2(in_6[26]), .E18(1'b0), .E3(in_6[27]),
    .E19(1'b0), .E4(in_6[28]), .E20(1'b0), .E5(in_6[29]), .E21(1'b0), .E6(in_6[30]), .E22(1'b0),
    .E7(in_6[31]), .E23(1'b0), .E8(1'b0), .E24(1'b0), .E9(1'b0), .E25(1'b0), .E10(1'b0), .E26(1'b0),
    .E11(1'b0), .E27(1'b0), .E12(1'b0), .E28(1'b0), .E13(1'b0), .E29(1'b0), .E14(1'b0), .E30(1'b0),
    .E15(1'b0), .E31(1'b0), .in_37(C0), .in_33(C1), .in_34(C2), .in_35(C3), .S(out_7[24]), .in_36(C4));
  Mux32_com_Mux16 _1 (
    .E0(in_6[1]), .E16(in_6[17]), .E1(in_6[2]), .E17(in_6[18]), .E2(in_6[3]), .E18(in_6[19]), .E3(in_6[4]),
    .E19(in_6[20]), .E4(in_6[5]), .E20(in_6[21]), .E5(in_6[6]), .E21(in_6[22]), .E6(in_6[7]), .E22(in_6[23]),
    .E7(in_6[8]), .E23(in_6[24]), .E8(in_6[9]), .E24(in_6[25]), .E9(in_6[10]), .E25(in_6[26]),
    .E10(in_6[11]), .E26(in_6[27]), .E11(in_6[12]), .E27(in_6[28]), .E12(in_6[13]), .E28(in_6[29]),
    .E13(in_6[14]), .E29(in_6[30]), .E14(in_6[15]), .E30(in_6[31]), .E15(in_6[16]), .E31(1'b0), .in_37(C0),
    .in_33(C1), .in_34(C2), .in_35(C3), .S(out_7[1]), .in_36(C4));
  Mux32_com_Mux16 _9 (
    .E0(in_6[9]), .E16(in_6[25]), .E1(in_6[10]), .E17(in_6[26]), .E2(in_6[11]), .E18(in_6[27]),
    .E3(in_6[12]), .E19(in_6[28]), .E4(in_6[13]), .E20(in_6[29]), .E5(in_6[14]), .E21(in_6[30]),
    .E6(in_6[15]), .E22(in_6[31]), .E7(in_6[16]), .E23(1'b0), .E8(in_6[17]), .E24(1'b0), .E9(in_6[18]),
    .E25(1'b0), .E10(in_6[19]), .E26(1'b0), .E11(in_6[20]), .E27(1'b0), .E12(in_6[21]), .E28(1'b0),
    .E13(in_6[22]), .E29(1'b0), .E14(in_6[23]), .E30(1'b0), .E15(in_6[24]), .E31(1'b0), .in_37(C0),
    .in_33(C1), .in_34(C2), .in_35(C3), .S(out_7[9]), .in_36(C4));
  Mux32_com_Mux16 _17 (
    .E0(in_6[17]), .E16(1'b0), .E1(in_6[18]), .E17(1'b0), .E2(in_6[19]), .E18(1'b0), .E3(in_6[20]),
    .E19(1'b0), .E4(in_6[21]), .E20(1'b0), .E5(in_6[22]), .E21(1'b0), .E6(in_6[23]), .E22(1'b0),
    .E7(in_6[24]), .E23(1'b0), .E8(in_6[25]), .E24(1'b0), .E9(in_6[26]), .E25(1'b0), .E10(in_6[27]),
    .E26(1'b0), .E11(in_6[28]), .E27(1'b0), .E12(in_6[29]), .E28(1'b0), .E13(in_6[30]), .E29(1'b0),
    .E14(in_6[31]), .E30(1'b0), .E15(1'b0), .E31(1'b0), .in_37(C0), .in_33(C1), .in_34(C2), .in_35(C3),
    .S(out_7[17]), .in_36(C4));
  Mux32_com_Mux16 _25 (
    .E0(in_6[25]), .E16(1'b0), .E1(in_6[26]), .E17(1'b0), .E2(in_6[27]), .E18(1'b0), .E3(in_6[28]),
    .E19(1'b0), .E4(in_6[29]), .E20(1'b0), .E5(in_6[30]), .E21(1'b0), .E6(in_6[31]), .E22(1'b0), .E7(1'b0),
    .E23(1'b0), .E8(1'b0), .E24(1'b0), .E9(1'b0), .E25(1'b0), .E10(1'b0), .E26(1'b0), .E11(1'b0), .E27(1'b0),
    .E12(1'b0), .E28(1'b0), .E13(1'b0), .E29(1'b0), .E14(1'b0), .E30(1'b0), .E15(1'b0), .E31(1'b0),
    .in_37(C0), .in_33(C1), .in_34(C2), .in_35(C3), .S(out_7[25]), .in_36(C4));
  Mux32_com_Mux16 _2 (
    .E0(in_6[2]), .E16(in_6[18]), .E1(in_6[3]), .E17(in_6[19]), .E2(in_6[4]), .E18(in_6[20]), .E3(in_6[5]),
    .E19(in_6[21]), .E4(in_6[6]), .E20(in_6[22]), .E5(in_6[7]), .E21(in_6[23]), .E6(in_6[8]), .E22(in_6[24]),
    .E7(in_6[9]), .E23(in_6[25]), .E8(in_6[10]), .E24(in_6[26]), .E9(in_6[11]), .E25(in_6[27]),
    .E10(in_6[12]), .E26(in_6[28]), .E11(in_6[13]), .E27(in_6[29]), .E12(in_6[14]), .E28(in_6[30]),
    .E13(in_6[15]), .E29(in_6[31]), .E14(in_6[16]), .E30(1'b0), .E15(in_6[17]), .E31(1'b0), .in_37(C0),
    .in_33(C1), .in_34(C2), .in_35(C3), .S(out_7[2]), .in_36(C4));
  Mux32_com_Mux16 _10 (
    .E0(in_6[10]), .E16(in_6[26]), .E1(in_6[11]), .E17(in_6[27]), .E2(in_6[12]), .E18(in_6[28]),
    .E3(in_6[13]), .E19(in_6[29]), .E4(in_6[14]), .E20(in_6[30]), .E5(in_6[15]), .E21(in_6[31]),
    .E6(in_6[16]), .E22(1'b0), .E7(in_6[17]), .E23(1'b0), .E8(in_6[18]), .E24(1'b0), .E9(in_6[19]),
    .E25(1'b0), .E10(in_6[20]), .E26(1'b0), .E11(in_6[21]), .E27(1'b0), .E12(in_6[22]), .E28(1'b0),
    .E13(in_6[23]), .E29(1'b0), .E14(in_6[24]), .E30(1'b0), .E15(in_6[25]), .E31(1'b0), .in_37(C0),
    .in_33(C1), .in_34(C2), .in_35(C3), .S(out_7[10]), .in_36(C4));
  Mux32_com_Mux16 _18 (
    .E0(in_6[18]), .E16(1'b0), .E1(in_6[19]), .E17(1'b0), .E2(in_6[20]), .E18(1'b0), .E3(in_6[21]),
    .E19(1'b0), .E4(in_6[22]), .E20(1'b0), .E5(in_6[23]), .E21(1'b0), .E6(in_6[24]), .E22(1'b0),
    .E7(in_6[25]), .E23(1'b0), .E8(in_6[26]), .E24(1'b0), .E9(in_6[27]), .E25(1'b0), .E10(in_6[28]),
    .E26(1'b0), .E11(in_6[29]), .E27(1'b0), .E12(in_6[30]), .E28(1'b0), .E13(in_6[31]), .E29(1'b0),
    .E14(1'b0), .E30(1'b0), .E15(1'b0), .E31(1'b0), .in_37(C0), .in_33(C1), .in_34(C2), .in_35(C3),
    .S(out_7[18]), .in_36(C4));
  Mux32_com_Mux16 _26 (
    .E0(in_6[26]), .E16(1'b0), .E1(in_6[27]), .E17(1'b0), .E2(in_6[28]), .E18(1'b0), .E3(in_6[29]),
    .E19(1'b0), .E4(in_6[30]), .E20(1'b0), .E5(in_6[31]), .E21(1'b0), .E6(1'b0), .E22(1'b0), .E7(1'b0),
    .E23(1'b0), .E8(1'b0), .E24(1'b0), .E9(1'b0), .E25(1'b0), .E10(1'b0), .E26(1'b0), .E11(1'b0), .E27(1'b0),
    .E12(1'b0), .E28(1'b0), .E13(1'b0), .E29(1'b0), .E14(1'b0), .E30(1'b0), .E15(1'b0), .E31(1'b0),
    .in_37(C0), .in_33(C1), .in_34(C2), .in_35(C3), .S(out_7[26]), .in_36(C4));
  Mux32_com_Mux16 _3 (
    .E0(in_6[3]), .E16(in_6[19]), .E1(in_6[4]), .E17(in_6[20]), .E2(in_6[5]), .E18(in_6[21]), .E3(in_6[6]),
    .E19(in_6[22]), .E4(in_6[7]), .E20(in_6[23]), .E5(in_6[8]), .E21(in_6[24]), .E6(in_6[9]), .E22(in_6[25]),
    .E7(in_6[10]), .E23(in_6[26]), .E8(in_6[11]), .E24(in_6[27]), .E9(in_6[12]), .E25(in_6[28]),
    .E10(in_6[13]), .E26(in_6[29]), .E11(in_6[14]), .E27(in_6[30]), .E12(in_6[15]), .E28(in_6[31]),
    .E13(in_6[16]), .E29(1'b0), .E14(in_6[17]), .E30(1'b0), .E15(in_6[18]), .E31(1'b0), .in_37(C0),
    .in_33(C1), .in_34(C2), .in_35(C3), .S(out_7[3]), .in_36(C4));
  Mux32_com_Mux16 _11 (
    .E0(in_6[11]), .E16(in_6[27]), .E1(in_6[12]), .E17(in_6[28]), .E2(in_6[13]), .E18(in_6[29]),
    .E3(in_6[14]), .E19(in_6[30]), .E4(in_6[15]), .E20(in_6[31]), .E5(in_6[16]), .E21(1'b0), .E6(in_6[17]),
    .E22(1'b0), .E7(in_6[18]), .E23(1'b0), .E8(in_6[19]), .E24(1'b0), .E9(in_6[20]), .E25(1'b0),
    .E10(in_6[21]), .E26(1'b0), .E11(in_6[22]), .E27(1'b0), .E12(in_6[23]), .E28(1'b0), .E13(in_6[24]),
    .E29(1'b0), .E14(in_6[25]), .E30(1'b0), .E15(in_6[26]), .E31(1'b0), .in_37(C0), .in_33(C1), .in_34(C2),
    .in_35(C3), .S(out_7[11]), .in_36(C4));
  Mux32_com_Mux16 _19 (
    .E0(in_6[19]), .E16(1'b0), .E1(in_6[20]), .E17(1'b0), .E2(in_6[21]), .E18(1'b0), .E3(in_6[22]),
    .E19(1'b0), .E4(in_6[23]), .E20(1'b0), .E5(in_6[24]), .E21(1'b0), .E6(in_6[25]), .E22(1'b0),
    .E7(in_6[26]), .E23(1'b0), .E8(in_6[27]), .E24(1'b0), .E9(in_6[28]), .E25(1'b0), .E10(in_6[29]),
    .E26(1'b0), .E11(in_6[30]), .E27(1'b0), .E12(in_6[31]), .E28(1'b0), .E13(1'b0), .E29(1'b0), .E14(1'b0),
    .E30(1'b0), .E15(1'b0), .E31(1'b0), .in_37(C0), .in_33(C1), .in_34(C2), .in_35(C3), .S(out_7[19]),
    .in_36(C4));
  Mux32_com_Mux16 _27 (
    .E0(in_6[27]), .E16(1'b0), .E1(in_6[28]), .E17(1'b0), .E2(in_6[29]), .E18(1'b0), .E3(in_6[30]),
    .E19(1'b0), .E4(in_6[31]), .E20(1'b0), .E5(1'b0), .E21(1'b0), .E6(1'b0), .E22(1'b0), .E7(1'b0),
    .E23(1'b0), .E8(1'b0), .E24(1'b0), .E9(1'b0), .E25(1'b0), .E10(1'b0), .E26(1'b0), .E11(1'b0), .E27(1'b0),
    .E12(1'b0), .E28(1'b0), .E13(1'b0), .E29(1'b0), .E14(1'b0), .E30(1'b0), .E15(1'b0), .E31(1'b0),
    .in_37(C0), .in_33(C1), .in_34(C2), .in_35(C3), .S(out_7[27]), .in_36(C4));
  Mux32_com_Mux16 _4 (
    .E0(in_6[4]), .E16(in_6[20]), .E1(in_6[5]), .E17(in_6[21]), .E2(in_6[6]), .E18(in_6[22]), .E3(in_6[7]),
    .E19(in_6[23]), .E4(in_6[8]), .E20(in_6[24]), .E5(in_6[9]), .E21(in_6[25]), .E6(in_6[10]),
    .E22(in_6[26]), .E7(in_6[11]), .E23(in_6[27]), .E8(in_6[12]), .E24(in_6[28]), .E9(in_6[13]),
    .E25(in_6[29]), .E10(in_6[14]), .E26(in_6[30]), .E11(in_6[15]), .E27(in_6[31]), .E12(in_6[16]),
    .E28(1'b0), .E13(in_6[17]), .E29(1'b0), .E14(in_6[18]), .E30(1'b0), .E15(in_6[19]), .E31(1'b0),
    .in_37(C0), .in_33(C1), .in_34(C2), .in_35(C3), .S(out_7[4]), .in_36(C4));
  Mux32_com_Mux16 _12 (
    .E0(in_6[12]), .E16(in_6[28]), .E1(in_6[13]), .E17(in_6[29]), .E2(in_6[14]), .E18(in_6[30]),
    .E3(in_6[15]), .E19(in_6[31]), .E4(in_6[16]), .E20(1'b0), .E5(in_6[17]), .E21(1'b0), .E6(in_6[18]),
    .E22(1'b0), .E7(in_6[19]), .E23(1'b0), .E8(in_6[20]), .E24(1'b0), .E9(in_6[21]), .E25(1'b0),
    .E10(in_6[22]), .E26(1'b0), .E11(in_6[23]), .E27(1'b0), .E12(in_6[24]), .E28(1'b0), .E13(in_6[25]),
    .E29(1'b0), .E14(in_6[26]), .E30(1'b0), .E15(in_6[27]), .E31(1'b0), .in_37(C0), .in_33(C1), .in_34(C2),
    .in_35(C3), .S(out_7[12]), .in_36(C4));
  Mux32_com_Mux16 _20 (
    .E0(in_6[20]), .E16(1'b0), .E1(in_6[21]), .E17(1'b0), .E2(in_6[22]), .E18(1'b0), .E3(in_6[23]),
    .E19(1'b0), .E4(in_6[24]), .E20(1'b0), .E5(in_6[25]), .E21(1'b0), .E6(in_6[26]), .E22(1'b0),
    .E7(in_6[27]), .E23(1'b0), .E8(in_6[28]), .E24(1'b0), .E9(in_6[29]), .E25(1'b0), .E10(in_6[30]),
    .E26(1'b0), .E11(in_6[31]), .E27(1'b0), .E12(1'b0), .E28(1'b0), .E13(1'b0), .E29(1'b0), .E14(1'b0),
    .E30(1'b0), .E15(1'b0), .E31(1'b0), .in_37(C0), .in_33(C1), .in_34(C2), .in_35(C3), .S(out_7[20]),
    .in_36(C4));
  Mux32_com_Mux16 _28 (
    .E0(in_6[28]), .E16(1'b0), .E1(in_6[29]), .E17(1'b0), .E2(in_6[30]), .E18(1'b0), .E3(in_6[31]),
    .E19(1'b0), .E4(1'b0), .E20(1'b0), .E5(1'b0), .E21(1'b0), .E6(1'b0), .E22(1'b0), .E7(1'b0), .E23(1'b0),
    .E8(1'b0), .E24(1'b0), .E9(1'b0), .E25(1'b0), .E10(1'b0), .E26(1'b0), .E11(1'b0), .E27(1'b0), .E12(1'b0),
    .E28(1'b0), .E13(1'b0), .E29(1'b0), .E14(1'b0), .E30(1'b0), .E15(1'b0), .E31(1'b0), .in_37(C0),
    .in_33(C1), .in_34(C2), .in_35(C3), .S(out_7[28]), .in_36(C4));
  Mux32_com_Mux16 _5 (
    .E0(in_6[5]), .E16(in_6[21]), .E1(in_6[6]), .E17(in_6[22]), .E2(in_6[7]), .E18(in_6[23]), .E3(in_6[8]),
    .E19(in_6[24]), .E4(in_6[9]), .E20(in_6[25]), .E5(in_6[10]), .E21(in_6[26]), .E6(in_6[11]),
    .E22(in_6[27]), .E7(in_6[12]), .E23(in_6[28]), .E8(in_6[13]), .E24(in_6[29]), .E9(in_6[14]),
    .E25(in_6[30]), .E10(in_6[15]), .E26(in_6[31]), .E11(in_6[16]), .E27(1'b0), .E12(in_6[17]), .E28(1'b0),
    .E13(in_6[18]), .E29(1'b0), .E14(in_6[19]), .E30(1'b0), .E15(in_6[20]), .E31(1'b0), .in_37(C0),
    .in_33(C1), .in_34(C2), .in_35(C3), .S(out_7[5]), .in_36(C4));
  Mux32_com_Mux16 _13 (
    .E0(in_6[13]), .E16(in_6[29]), .E1(in_6[14]), .E17(in_6[30]), .E2(in_6[15]), .E18(in_6[31]),
    .E3(in_6[16]), .E19(1'b0), .E4(in_6[17]), .E20(1'b0), .E5(in_6[18]), .E21(1'b0), .E6(in_6[19]),
    .E22(1'b0), .E7(in_6[20]), .E23(1'b0), .E8(in_6[21]), .E24(1'b0), .E9(in_6[22]), .E25(1'b0),
    .E10(in_6[23]), .E26(1'b0), .E11(in_6[24]), .E27(1'b0), .E12(in_6[25]), .E28(1'b0), .E13(in_6[26]),
    .E29(1'b0), .E14(in_6[27]), .E30(1'b0), .E15(in_6[28]), .E31(1'b0), .in_37(C0), .in_33(C1), .in_34(C2),
    .in_35(C3), .S(out_7[13]), .in_36(C4));
  Mux32_com_Mux16 _21 (
    .E0(in_6[21]), .E16(1'b0), .E1(in_6[22]), .E17(1'b0), .E2(in_6[23]), .E18(1'b0), .E3(in_6[24]),
    .E19(1'b0), .E4(in_6[25]), .E20(1'b0), .E5(in_6[26]), .E21(1'b0), .E6(in_6[27]), .E22(1'b0),
    .E7(in_6[28]), .E23(1'b0), .E8(in_6[29]), .E24(1'b0), .E9(in_6[30]), .E25(1'b0), .E10(in_6[31]),
    .E26(1'b0), .E11(1'b0), .E27(1'b0), .E12(1'b0), .E28(1'b0), .E13(1'b0), .E29(1'b0), .E14(1'b0),
    .E30(1'b0), .E15(1'b0), .E31(1'b0), .in_37(C0), .in_33(C1), .in_34(C2), .in_35(C3), .S(out_7[21]),
    .in_36(C4));
  Mux32_com_Mux16 _29 (
    .E0(in_6[29]), .E16(1'b0), .E1(in_6[30]), .E17(1'b0), .E2(in_6[31]), .E18(1'b0), .E3(1'b0), .E19(1'b0),
    .E4(1'b0), .E20(1'b0), .E5(1'b0), .E21(1'b0), .E6(1'b0), .E22(1'b0), .E7(1'b0), .E23(1'b0), .E8(1'b0),
    .E24(1'b0), .E9(1'b0), .E25(1'b0), .E10(1'b0), .E26(1'b0), .E11(1'b0), .E27(1'b0), .E12(1'b0),
    .E28(1'b0), .E13(1'b0), .E29(1'b0), .E14(1'b0), .E30(1'b0), .E15(1'b0), .E31(1'b0), .in_37(C0),
    .in_33(C1), .in_34(C2), .in_35(C3), .S(out_7[29]), .in_36(C4));
  Mux32_com_Mux16 _6 (
    .E0(in_6[6]), .E16(in_6[22]), .E1(in_6[7]), .E17(in_6[23]), .E2(in_6[8]), .E18(in_6[24]), .E3(in_6[9]),
    .E19(in_6[25]), .E4(in_6[10]), .E20(in_6[26]), .E5(in_6[11]), .E21(in_6[27]), .E6(in_6[12]),
    .E22(in_6[28]), .E7(in_6[13]), .E23(in_6[29]), .E8(in_6[14]), .E24(in_6[30]), .E9(in_6[15]),
    .E25(in_6[31]), .E10(in_6[16]), .E26(1'b0), .E11(in_6[17]), .E27(1'b0), .E12(in_6[18]), .E28(1'b0),
    .E13(in_6[19]), .E29(1'b0), .E14(in_6[20]), .E30(1'b0), .E15(in_6[21]), .E31(1'b0), .in_37(C0),
    .in_33(C1), .in_34(C2), .in_35(C3), .S(out_7[6]), .in_36(C4));
  Mux32_com_Mux16 _14 (
    .E0(in_6[14]), .E16(in_6[30]), .E1(in_6[15]), .E17(in_6[31]), .E2(in_6[16]), .E18(1'b0), .E3(in_6[17]),
    .E19(1'b0), .E4(in_6[18]), .E20(1'b0), .E5(in_6[19]), .E21(1'b0), .E6(in_6[20]), .E22(1'b0),
    .E7(in_6[21]), .E23(1'b0), .E8(in_6[22]), .E24(1'b0), .E9(in_6[23]), .E25(1'b0), .E10(in_6[24]),
    .E26(1'b0), .E11(in_6[25]), .E27(1'b0), .E12(in_6[26]), .E28(1'b0), .E13(in_6[27]), .E29(1'b0),
    .E14(in_6[28]), .E30(1'b0), .E15(in_6[29]), .E31(1'b0), .in_37(C0), .in_33(C1), .in_34(C2), .in_35(C3),
    .S(out_7[14]), .in_36(C4));
  Mux32_com_Mux16 _22 (
    .E0(in_6[22]), .E16(1'b0), .E1(in_6[23]), .E17(1'b0), .E2(in_6[24]), .E18(1'b0), .E3(in_6[25]),
    .E19(1'b0), .E4(in_6[26]), .E20(1'b0), .E5(in_6[27]), .E21(1'b0), .E6(in_6[28]), .E22(1'b0),
    .E7(in_6[29]), .E23(1'b0), .E8(in_6[30]), .E24(1'b0), .E9(in_6[31]), .E25(1'b0), .E10(1'b0), .E26(1'b0),
    .E11(1'b0), .E27(1'b0), .E12(1'b0), .E28(1'b0), .E13(1'b0), .E29(1'b0), .E14(1'b0), .E30(1'b0),
    .E15(1'b0), .E31(1'b0), .in_37(C0), .in_33(C1), .in_34(C2), .in_35(C3), .S(out_7[22]), .in_36(C4));
  Mux32_com_Mux16 _30 (
    .E0(in_6[30]), .E16(1'b0), .E1(in_6[31]), .E17(1'b0), .E2(1'b0), .E18(1'b0), .E3(1'b0), .E19(1'b0),
    .E4(1'b0), .E20(1'b0), .E5(1'b0), .E21(1'b0), .E6(1'b0), .E22(1'b0), .E7(1'b0), .E23(1'b0), .E8(1'b0),
    .E24(1'b0), .E9(1'b0), .E25(1'b0), .E10(1'b0), .E26(1'b0), .E11(1'b0), .E27(1'b0), .E12(1'b0),
    .E28(1'b0), .E13(1'b0), .E29(1'b0), .E14(1'b0), .E30(1'b0), .E15(1'b0), .E31(1'b0), .in_37(C0),
    .in_33(C1), .in_34(C2), .in_35(C3), .S(out_7[30]), .in_36(C4));
  Mux32_com_Mux16 _7 (
    .E0(in_6[7]), .E16(in_6[23]), .E1(in_6[8]), .E17(in_6[24]), .E2(in_6[9]), .E18(in_6[25]), .E3(in_6[10]),
    .E19(in_6[26]), .E4(in_6[11]), .E20(in_6[27]), .E5(in_6[12]), .E21(in_6[28]), .E6(in_6[13]),
    .E22(in_6[29]), .E7(in_6[14]), .E23(in_6[30]), .E8(in_6[15]), .E24(in_6[31]), .E9(in_6[16]), .E25(1'b0),
    .E10(in_6[17]), .E26(1'b0), .E11(in_6[18]), .E27(1'b0), .E12(in_6[19]), .E28(1'b0), .E13(in_6[20]),
    .E29(1'b0), .E14(in_6[21]), .E30(1'b0), .E15(in_6[22]), .E31(1'b0), .in_37(C0), .in_33(C1), .in_34(C2),
    .in_35(C3), .S(out_7[7]), .in_36(C4));
  Mux32_com_Mux16 _15 (
    .E0(in_6[15]), .E16(in_6[31]), .E1(in_6[16]), .E17(1'b0), .E2(in_6[17]), .E18(1'b0), .E3(in_6[18]),
    .E19(1'b0), .E4(in_6[19]), .E20(1'b0), .E5(in_6[20]), .E21(1'b0), .E6(in_6[21]), .E22(1'b0),
    .E7(in_6[22]), .E23(1'b0), .E8(in_6[23]), .E24(1'b0), .E9(in_6[24]), .E25(1'b0), .E10(in_6[25]),
    .E26(1'b0), .E11(in_6[26]), .E27(1'b0), .E12(in_6[27]), .E28(1'b0), .E13(in_6[28]), .E29(1'b0),
    .E14(in_6[29]), .E30(1'b0), .E15(in_6[30]), .E31(1'b0), .in_37(C0), .in_33(C1), .in_34(C2), .in_35(C3),
    .S(out_7[15]), .in_36(C4));
  Mux32_com_Mux16 _23 (
    .E0(in_6[23]), .E16(1'b0), .E1(in_6[24]), .E17(1'b0), .E2(in_6[25]), .E18(1'b0), .E3(in_6[26]),
    .E19(1'b0), .E4(in_6[27]), .E20(1'b0), .E5(in_6[28]), .E21(1'b0), .E6(in_6[29]), .E22(1'b0),
    .E7(in_6[30]), .E23(1'b0), .E8(in_6[31]), .E24(1'b0), .E9(1'b0), .E25(1'b0), .E10(1'b0), .E26(1'b0),
    .E11(1'b0), .E27(1'b0), .E12(1'b0), .E28(1'b0), .E13(1'b0), .E29(1'b0), .E14(1'b0), .E30(1'b0),
    .E15(1'b0), .E31(1'b0), .in_37(C0), .in_33(C1), .in_34(C2), .in_35(C3), .S(out_7[23]), .in_36(C4));
  Mux32_com_Mux16 _31 (
    .E0(in_6[31]), .E16(1'b0), .E1(1'b0), .E17(1'b0), .E2(1'b0), .E18(1'b0), .E3(1'b0), .E19(1'b0),
    .E4(1'b0), .E20(1'b0), .E5(1'b0), .E21(1'b0), .E6(1'b0), .E22(1'b0), .E7(1'b0), .E23(1'b0), .E8(1'b0),
    .E24(1'b0), .E9(1'b0), .E25(1'b0), .E10(1'b0), .E26(1'b0), .E11(1'b0), .E27(1'b0), .E12(1'b0),
    .E28(1'b0), .E13(1'b0), .E29(1'b0), .E14(1'b0), .E30(1'b0), .E15(1'b0), .E31(1'b0), .in_37(C0),
    .in_33(C1), .in_34(C2), .in_35(C3), .S(out_7[31]), .in_36(C4));
endmodule

module Deslocador (
  input  [31:0] A_B,
  input  in_2,
  input  [4:0] in_3,
  output [31:0] A_prime_B_prime
);

  wire [31:0] left_shifter_1_out_7, right_shifter_1_out_7;

  Left_Shifter left_shifter_1 (
    .in_6(A_B), .out_7(left_shifter_1_out_7), .C0(in_3[4]), .C1(in_3[3]), .C2(in_3[2]), .C3(in_3[1]),
    .C4(in_3[0]));
  Right_shifter right_shifter_1 (
    .in_6(A_B), .out_7(right_shifter_1_out_7), .C0(in_3[4]), .C1(in_3[3]), .C2(in_3[2]), .C3(in_3[1]),
    .C4(in_3[0]));
  MUX2___32 mux2_32_1 (.in_1(left_shifter_1_out_7), .in_2(right_shifter_1_out_7), .in_3(in_2), .out_4(A_prime_B_prime));
endmodule

module Reg (
  input  [31:0] RegIN,
  input  WR,
  output [31:0] DataINRelay,
  output [31:0] out_4
);

  D_Flip_Flop _31 (.clk(WR), .D(RegIN[31]), .Q(out_4[31]));  // open: Qn, preset, en, reset
  D_Flip_Flop _23 (.clk(WR), .D(RegIN[23]), .Q(out_4[23]));  // open: Qn, preset, en, reset
  D_Flip_Flop _15 (.clk(WR), .D(RegIN[15]), .Q(out_4[15]));  // open: Qn, preset, en, reset
  D_Flip_Flop _7 (.clk(WR), .D(RegIN[7]), .Q(out_4[7]));  // open: Qn, preset, en, reset
  D_Flip_Flop _30 (.clk(WR), .D(RegIN[30]), .Q(out_4[30]));  // open: Qn, preset, en, reset
  D_Flip_Flop _22 (.clk(WR), .D(RegIN[22]), .Q(out_4[22]));  // open: Qn, preset, en, reset
  D_Flip_Flop _14 (.clk(WR), .D(RegIN[14]), .Q(out_4[14]));  // open: Qn, preset, en, reset
  D_Flip_Flop _6 (.clk(WR), .D(RegIN[6]), .Q(out_4[6]));  // open: Qn, preset, en, reset
  D_Flip_Flop _29 (.clk(WR), .D(RegIN[29]), .Q(out_4[29]));  // open: Qn, preset, en, reset
  D_Flip_Flop _21 (.clk(WR), .D(RegIN[21]), .Q(out_4[21]));  // open: Qn, preset, en, reset
  D_Flip_Flop _13 (.clk(WR), .D(RegIN[13]), .Q(out_4[13]));  // open: Qn, preset, en, reset
  D_Flip_Flop _5 (.clk(WR), .D(RegIN[5]), .Q(out_4[5]));  // open: Qn, preset, en, reset
  D_Flip_Flop _28 (.clk(WR), .D(RegIN[28]), .Q(out_4[28]));  // open: Qn, preset, en, reset
  D_Flip_Flop _20 (.clk(WR), .D(RegIN[20]), .Q(out_4[20]));  // open: Qn, preset, en, reset
  D_Flip_Flop _12 (.clk(WR), .D(RegIN[12]), .Q(out_4[12]));  // open: Qn, preset, en, reset
  D_Flip_Flop _4 (.clk(WR), .D(RegIN[4]), .Q(out_4[4]));  // open: Qn, preset, en, reset
  D_Flip_Flop _27 (.clk(WR), .D(RegIN[27]), .Q(out_4[27]));  // open: Qn, preset, en, reset
  D_Flip_Flop _19 (.clk(WR), .D(RegIN[19]), .Q(out_4[19]));  // open: Qn, preset, en, reset
  D_Flip_Flop _11 (.clk(WR), .D(RegIN[11]), .Q(out_4[11]));  // open: Qn, preset, en, reset
  D_Flip_Flop _3 (.clk(WR), .D(RegIN[3]), .Q(out_4[3]));  // open: Qn, preset, en, reset
  D_Flip_Flop _26 (.clk(WR), .D(RegIN[26]), .Q(out_4[26]));  // open: Qn, preset, en, reset
  D_Flip_Flop _18 (.clk(WR), .D(RegIN[18]), .Q(out_4[18]));  // open: Qn, preset, en, reset
  D_Flip_Flop _10 (.clk(WR), .D(RegIN[10]), .Q(out_4[10]));  // open: Qn, preset, en, reset
  D_Flip_Flop _2 (.clk(WR), .D(RegIN[2]), .Q(out_4[2]));  // open: Qn, preset, en, reset
  D_Flip_Flop _25 (.clk(WR), .D(RegIN[25]), .Q(out_4[25]));  // open: Qn, preset, en, reset
  D_Flip_Flop _17 (.clk(WR), .D(RegIN[17]), .Q(out_4[17]));  // open: Qn, preset, en, reset
  D_Flip_Flop _9 (.clk(WR), .D(RegIN[9]), .Q(out_4[9]));  // open: Qn, preset, en, reset
  D_Flip_Flop _1 (.clk(WR), .D(RegIN[1]), .Q(out_4[1]));  // open: Qn, preset, en, reset
  D_Flip_Flop _24 (.clk(WR), .D(RegIN[24]), .Q(out_4[24]));  // open: Qn, preset, en, reset
  D_Flip_Flop _16 (.clk(WR), .D(RegIN[16]), .Q(out_4[16]));  // open: Qn, preset, en, reset
  D_Flip_Flop _8 (.clk(WR), .D(RegIN[8]), .Q(out_4[8]));  // open: Qn, preset, en, reset
  D_Flip_Flop _0 (.clk(WR), .D(RegIN[0]), .Q(out_4[0]));  // open: Qn, preset, en, reset

  assign DataINRelay = RegIN;
endmodule

module Registrador (
  input  WR,
  input  [4:0] RegWR,
  input  [31:0] RegIN,
  input  [4:0] RegDATA_A,
  input  [4:0] RegDATA_B,
  output [31:0] DataINRelay,
  output [31:0] DATAReg_B,
  output [31:0] DATAReg_A
);

  wire demultiplexer_1_out0, demultiplexer_1_out1, demultiplexer_1_out2, demultiplexer_1_out3,
       demultiplexer_1_out4, demultiplexer_1_out5, demultiplexer_1_out6, demultiplexer_1_out7,
       demultiplexer_1_out8, demultiplexer_1_out9, demultiplexer_1_out10, demultiplexer_1_out11,
       demultiplexer_1_out12, demultiplexer_1_out13, demultiplexer_1_out14, demultiplexer_1_out15,
       demultiplexer_1_out16, demultiplexer_1_out17, demultiplexer_1_out18, demultiplexer_1_out19,
       demultiplexer_1_out20, demultiplexer_1_out21, demultiplexer_1_out22, demultiplexer_1_out23,
       demultiplexer_1_out24, demultiplexer_1_out25, demultiplexer_1_out26, demultiplexer_1_out27,
       demultiplexer_1_out28, demultiplexer_1_out29, demultiplexer_1_out30, demultiplexer_1_out31;
  wire [31:0] reg_1_out_4, reg_2_out_4, reg_3_out_4, reg_4_out_4, reg_5_out_4, reg_6_out_4, reg_7_out_4,
       reg_8_out_4, reg_9_out_4, reg_10_out_4, reg_11_out_4, reg_12_out_4, reg_13_out_4, reg_14_out_4,
       reg_15_out_4, reg_16_out_4, reg_17_out_4, reg_18_out_4, reg_19_out_4, reg_20_out_4, reg_21_out_4,
       reg_22_out_4, reg_23_out_4, reg_24_out_4, reg_25_out_4, reg_26_out_4, reg_27_out_4, reg_28_out_4,
       reg_29_out_4, reg_30_out_4, reg_31_out_4, reg_32_out_4;

  Demultiplexer #(.select(5)) demultiplexer_1 (
    .out0(demultiplexer_1_out0), .out1(demultiplexer_1_out1), .out2(demultiplexer_1_out2),
    .out3(demultiplexer_1_out3), .out4(demultiplexer_1_out4), .out5(demultiplexer_1_out5),
    .out6(demultiplexer_1_out6), .out7(demultiplexer_1_out7), .out8(demultiplexer_1_out8),
    .out9(demultiplexer_1_out9), .out10(demultiplexer_1_out10), .out11(demultiplexer_1_out11),
    .out12(demultiplexer_1_out12), .out13(demultiplexer_1_out13), .out14(demultiplexer_1_out14),
    .out15(demultiplexer_1_out15), .out16(demultiplexer_1_out16), .out17(demultiplexer_1_out17),
    .out18(demultiplexer_1_out18), .out19(demultiplexer_1_out19), .out20(demultiplexer_1_out20),
    .out21(demultiplexer_1_out21), .out22(demultiplexer_1_out22), .out23(demultiplexer_1_out23),
    .out24(demultiplexer_1_out24), .out25(demultiplexer_1_out25), .out26(demultiplexer_1_out26),
    .out27(demultiplexer_1_out27), .out28(demultiplexer_1_out28), .out29(demultiplexer_1_out29),
    .out30(demultiplexer_1_out30), .out31(demultiplexer_1_out31), .in(WR), .sel(RegWR));  // open: en
  Reg reg_1 (.WR(demultiplexer_1_out0), .RegIN(RegIN), .DataINRelay(DataINRelay), .out_4(reg_1_out_4));
  Reg reg_2 (.WR(demultiplexer_1_out8), .RegIN(RegIN), .DataINRelay(DataINRelay), .out_4(reg_2_out_4));
  Reg reg_3 (.WR(demultiplexer_1_out16), .RegIN(RegIN), .DataINRelay(DataINRelay), .out_4(reg_3_out_4));
  Reg reg_4 (.WR(demultiplexer_1_out24), .RegIN(RegIN), .DataINRelay(DataINRelay), .out_4(reg_4_out_4));
  Reg reg_5 (.WR(demultiplexer_1_out1), .RegIN(RegIN), .DataINRelay(DataINRelay), .out_4(reg_5_out_4));
  Reg reg_6 (.WR(demultiplexer_1_out9), .RegIN(RegIN), .DataINRelay(DataINRelay), .out_4(reg_6_out_4));
  Reg reg_7 (.WR(demultiplexer_1_out17), .RegIN(RegIN), .DataINRelay(DataINRelay), .out_4(reg_7_out_4));
  Reg reg_8 (.WR(demultiplexer_1_out25), .RegIN(RegIN), .DataINRelay(DataINRelay), .out_4(reg_8_out_4));
  Reg reg_9 (.WR(demultiplexer_1_out2), .RegIN(RegIN), .DataINRelay(DataINRelay), .out_4(reg_9_out_4));
  Reg reg_10 (.WR(demultiplexer_1_out10), .RegIN(RegIN), .DataINRelay(DataINRelay), .out_4(reg_10_out_4));
  Reg reg_11 (.WR(demultiplexer_1_out18), .RegIN(RegIN), .DataINRelay(DataINRelay), .out_4(reg_11_out_4));
  Reg reg_12 (.WR(demultiplexer_1_out26), .RegIN(RegIN), .DataINRelay(DataINRelay), .out_4(reg_12_out_4));
  Reg reg_13 (.WR(demultiplexer_1_out3), .RegIN(RegIN), .DataINRelay(DataINRelay), .out_4(reg_13_out_4));
  Reg reg_14 (.WR(demultiplexer_1_out11), .RegIN(RegIN), .DataINRelay(DataINRelay), .out_4(reg_14_out_4));
  Reg reg_15 (.WR(demultiplexer_1_out19), .RegIN(RegIN), .DataINRelay(DataINRelay), .out_4(reg_15_out_4));
  Reg reg_16 (.WR(demultiplexer_1_out27), .RegIN(RegIN), .DataINRelay(DataINRelay), .out_4(reg_16_out_4));
  Reg reg_17 (.WR(demultiplexer_1_out4), .RegIN(RegIN), .DataINRelay(DataINRelay), .out_4(reg_17_out_4));
  Reg reg_18 (.WR(demultiplexer_1_out12), .RegIN(RegIN), .DataINRelay(DataINRelay), .out_4(reg_18_out_4));
  Reg reg_19 (.WR(demultiplexer_1_out20), .RegIN(RegIN), .DataINRelay(DataINRelay), .out_4(reg_19_out_4));
  Reg reg_20 (.WR(demultiplexer_1_out28), .RegIN(RegIN), .DataINRelay(DataINRelay), .out_4(reg_20_out_4));
  Reg reg_21 (.WR(demultiplexer_1_out5), .RegIN(RegIN), .DataINRelay(DataINRelay), .out_4(reg_21_out_4));
  Reg reg_22 (.WR(demultiplexer_1_out13), .RegIN(RegIN), .DataINRelay(DataINRelay), .out_4(reg_22_out_4));
  Reg reg_23 (.WR(demultiplexer_1_out21), .RegIN(RegIN), .DataINRelay(DataINRelay), .out_4(reg_23_out_4));
  Reg reg_24 (.WR(demultiplexer_1_out29), .RegIN(RegIN), .DataINRelay(DataINRelay), .out_4(reg_24_out_4));
  Multiplexer #(.select(5), .width(32)) multiplexer_1 (
    .in0(reg_1_out_4), .in1(reg_5_out_4), .in2(reg_9_out_4), .in3(reg_13_out_4), .in4(reg_17_out_4),
    .in5(reg_21_out_4), .in6(reg_25_out_4), .in7(reg_29_out_4), .in8(reg_2_out_4), .in9(reg_6_out_4),
    .in10(reg_10_out_4), .in11(reg_14_out_4), .in12(reg_18_out_4), .in13(reg_22_out_4), .in14(reg_26_out_4),
    .in15(reg_30_out_4), .in16(reg_3_out_4), .in17(reg_7_out_4), .in18(reg_11_out_4), .in19(reg_15_out_4),
    .in20(reg_19_out_4), .in21(reg_23_out_4), .in22(reg_27_out_4), .in23(reg_31_out_4), .in24(reg_4_out_4),
    .in25(reg_8_out_4), .in26(reg_12_out_4), .in27(reg_16_out_4), .in28(reg_20_out_4), .in29(reg_24_out_4),
    .in30(reg_28_out_4), .in31(reg_32_out_4), .out(DATAReg_B), .sel(RegDATA_B));  // open: en
  Reg reg_25 (.WR(demultiplexer_1_out6), .RegIN(RegIN), .DataINRelay(DataINRelay), .out_4(reg_25_out_4));
  Reg reg_26 (.WR(demultiplexer_1_out14), .RegIN(RegIN), .DataINRelay(DataINRelay), .out_4(reg_26_out_4));
  Reg reg_27 (.WR(demultiplexer_1_out22), .RegIN(RegIN), .DataINRelay(DataINRelay), .out_4(reg_27_out_4));
  Reg reg_28 (.WR(demultiplexer_1_out30), .RegIN(RegIN), .DataINRelay(DataINRelay), .out_4(reg_28_out_4));
  Reg reg_29 (.WR(demultiplexer_1_out7), .RegIN(RegIN), .DataINRelay(DataINRelay), .out_4(reg_29_out_4));
  Reg reg_30 (.WR(demultiplexer_1_out15), .RegIN(RegIN), .DataINRelay(DataINRelay), .out_4(reg_30_out_4));
  Reg reg_31 (.WR(demultiplexer_1_out23), .RegIN(RegIN), .DataINRelay(DataINRelay), .out_4(reg_31_out_4));
  Reg reg_32 (.WR(demultiplexer_1_out31), .RegIN(RegIN), .DataINRelay(DataINRelay), .out_4(reg_32_out_4));
  Multiplexer #(.select(5), .width(32)) multiplexer_2 (
    .in0(reg_1_out_4), .in1(reg_5_out_4), .in2(reg_9_out_4), .in3(reg_13_out_4), .in4(reg_17_out_4),
    .in5(reg_21_out_4), .in6(reg_25_out_4), .in7(reg_29_out_4), .in8(reg_2_out_4), .in9(reg_6_out_4),
    .in10(reg_10_out_4), .in11(reg_14_out_4), .in12(reg_18_out_4), .in13(reg_22_out_4), .in14(reg_26_out_4),
    .in15(reg_30_out_4), .in16(reg_3_out_4), .in17(reg_7_out_4), .in18(reg_11_out_4), .in19(reg_15_out_4),
    .in20(reg_19_out_4), .in21(reg_23_out_4), .in22(reg_27_out_4), .in23(reg_31_out_4), .in24(reg_4_out_4),
    .in25(reg_8_out_4), .in26(reg_12_out_4), .in27(reg_16_out_4), .in28(reg_20_out_4), .in29(reg_24_out_4),
    .in30(reg_28_out_4), .in31(reg_32_out_4), .out(DATAReg_A), .sel(RegDATA_A));  // open: en
endmodule

module Via_de_dados (
  input  [31:0] \Instrução ,
  input  in_2,
  output out_3,
  output out_4
);

  wire unidade_de_controle_1_gera_e;
  wire [4:0] unidade_de_controle_1_opcode, unidade_de_controle_1_rega, unidade_de_controle_1_regb,
       unidade_de_controle_1_regw, unidade_de_controle_1_sa;
  wire [15:0] unidade_de_controle_1_dado_externo;
  wire [31:0] mux2_32_1_out_4, processador_1_s, registrador_1_datareg_a, registrador_1_datareg_b, undriven;

  Unidade_de_controle unidade_de_controle_1 (
    .\Instrução (\Instrução ), .Gera_E(unidade_de_controle_1_gera_e), .OpCode(unidade_de_controle_1_opcode),
    .RegA(unidade_de_controle_1_rega), .RegB(unidade_de_controle_1_regb), .RegW(unidade_de_controle_1_regw),
    .SA(unidade_de_controle_1_sa), .Dado_externo(unidade_de_controle_1_dado_externo));
  Registrador registrador_1 (
    .RegWR(unidade_de_controle_1_regw), .RegDATA_A(unidade_de_controle_1_rega), .WR(in_2),
    .RegIN(processador_1_s), .DATAReg_A(registrador_1_datareg_a), .RegDATA_B(unidade_de_controle_1_regb),
    .DATAReg_B(registrador_1_datareg_b));  // open: DataINRelay
  Extensor extensor_1 (.in_1(unidade_de_controle_1_dado_externo), .in_2(undriven));
  MUX2___32 mux2_32_1 (
    .in_1(registrador_1_datareg_b), .in_2(undriven), .in_3(unidade_de_controle_1_gera_e),
    .out_4(mux2_32_1_out_4));
  Processador processador_1 (
    .A(registrador_1_datareg_a), .B(mux2_32_1_out_4), .S(processador_1_s), .out_7(out_3), .out_9(out_4),
    .OpCode(unidade_de_controle_1_opcode), .Shift_Amount(unidade_de_controle_1_sa));  // open: Bin, L_R
endmodule

module Extensor (
  input  [15:0] in_1,
  input  [31:0] in_2
);


  assign in_2 = {{17{in_1[15]}}, in_1[14:0]};
endmodule

module Registradorr (
  input  WR,
  input  [4:0] RegWR,
  input  [31:0] RegIN,
  input  [4:0] RegDATA_A,
  output [31:0] DataINRelay,
  output [31:0] DATAReg_A
);

  wire demultiplexer_1_out0, demultiplexer_1_out1, demultiplexer_1_out2, demultiplexer_1_out3,
       demultiplexer_1_out4, demultiplexer_1_out5, demultiplexer_1_out6, demultiplexer_1_out7,
       demultiplexer_1_out8, demultiplexer_1_out9, demultiplexer_1_out10, demultiplexer_1_out11,
       demultiplexer_1_out12, demultiplexer_1_out13, demultiplexer_1_out14, demultiplexer_1_out15,
       demultiplexer_1_out16, demultiplexer_1_out17, demultiplexer_1_out18, demultiplexer_1_out19,
       demultiplexer_1_out20, demultiplexer_1_out21, demultiplexer_1_out22, demultiplexer_1_out23,
       demultiplexer_1_out24, demultiplexer_1_out25, demultiplexer_1_out26, demultiplexer_1_out27,
       demultiplexer_1_out28, demultiplexer_1_out29, demultiplexer_1_out30, demultiplexer_1_out31;
  wire [31:0] reg_1_out_4, reg_2_out_4, reg_3_out_4, reg_4_out_4, reg_5_out_4, reg_6_out_4, reg_7_out_4,
       reg_8_out_4, reg_9_out_4, reg_10_out_4, reg_11_out_4, reg_12_out_4, reg_13_out_4, reg_14_out_4,
       reg_15_out_4, reg_16_out_4, reg_17_out_4, reg_18_out_4, reg_19_out_4, reg_20_out_4, reg_21_out_4,
       reg_22_out_4, reg_23_out_4, reg_24_out_4, reg_25_out_4, reg_26_out_4, reg_27_out_4, reg_28_out_4,
       reg_29_out_4, reg_30_out_4, reg_31_out_4, reg_32_out_4;

  Demultiplexer #(.select(5)) demultiplexer_1 (
    .out0(demultiplexer_1_out0), .out1(demultiplexer_1_out1), .out2(demultiplexer_1_out2),
    .out3(demultiplexer_1_out3), .out4(demultiplexer_1_out4), .out5(demultiplexer_1_out5),
    .out6(demultiplexer_1_out6), .out7(demultiplexer_1_out7), .out8(demultiplexer_1_out8),
    .out9(demultiplexer_1_out9), .out10(demultiplexer_1_out10), .out11(demultiplexer_1_out11),
    .out12(demultiplexer_1_out12), .out13(demultiplexer_1_out13), .out14(demultiplexer_1_out14),
    .out15(demultiplexer_1_out15), .out16(demultiplexer_1_out16), .out17(demultiplexer_1_out17),
    .out18(demultiplexer_1_out18), .out19(demultiplexer_1_out19), .out20(demultiplexer_1_out20),
    .out21(demultiplexer_1_out21), .out22(demultiplexer_1_out22), .out23(demultiplexer_1_out23),
    .out24(demultiplexer_1_out24), .out25(demultiplexer_1_out25), .out26(demultiplexer_1_out26),
    .out27(demultiplexer_1_out27), .out28(demultiplexer_1_out28), .out29(demultiplexer_1_out29),
    .out30(demultiplexer_1_out30), .out31(demultiplexer_1_out31), .in(WR), .sel(RegWR));  // open: en
  Reg reg_1 (.WR(demultiplexer_1_out0), .RegIN(RegIN), .DataINRelay(DataINRelay), .out_4(reg_1_out_4));
  Reg reg_2 (.WR(demultiplexer_1_out8), .RegIN(RegIN), .DataINRelay(DataINRelay), .out_4(reg_2_out_4));
  Reg reg_3 (.WR(demultiplexer_1_out16), .RegIN(RegIN), .DataINRelay(DataINRelay), .out_4(reg_3_out_4));
  Reg reg_4 (.WR(demultiplexer_1_out24), .RegIN(RegIN), .DataINRelay(DataINRelay), .out_4(reg_4_out_4));
  Reg reg_5 (.WR(demultiplexer_1_out1), .RegIN(RegIN), .DataINRelay(DataINRelay), .out_4(reg_5_out_4));
  Reg reg_6 (.WR(demultiplexer_1_out9), .RegIN(RegIN), .DataINRelay(DataINRelay), .out_4(reg_6_out_4));
  Reg reg_7 (.WR(demultiplexer_1_out17), .RegIN(RegIN), .DataINRelay(DataINRelay), .out_4(reg_7_out_4));
  Reg reg_8 (.WR(demultiplexer_1_out25), .RegIN(RegIN), .DataINRelay(DataINRelay), .out_4(reg_8_out_4));
  Reg reg_9 (.WR(demultiplexer_1_out2), .RegIN(RegIN), .DataINRelay(DataINRelay), .out_4(reg_9_out_4));
  Reg reg_10 (.WR(demultiplexer_1_out10), .RegIN(RegIN), .DataINRelay(DataINRelay), .out_4(reg_10_out_4));
  Reg reg_11 (.WR(demultiplexer_1_out18), .RegIN(RegIN), .DataINRelay(DataINRelay), .out_4(reg_11_out_4));
  Reg reg_12 (.WR(demultiplexer_1_out26), .RegIN(RegIN), .DataINRelay(DataINRelay), .out_4(reg_12_out_4));
  Reg reg_13 (.WR(demultiplexer_1_out3), .RegIN(RegIN), .DataINRelay(DataINRelay), .out_4(reg_13_out_4));
  Reg reg_14 (.WR(demultiplexer_1_out11), .RegIN(RegIN), .DataINRelay(DataINRelay), .out_4(reg_14_out_4));
  Reg reg_15 (.WR(demultiplexer_1_out19), .RegIN(RegIN), .DataINRelay(DataINRelay), .out_4(reg_15_out_4));
  Reg reg_16 (.WR(demultiplexer_1_out27), .RegIN(RegIN), .DataINRelay(DataINRelay), .out_4(reg_16_out_4));
  Reg reg_17 (.WR(demultiplexer_1_out4), .RegIN(RegIN), .DataINRelay(DataINRelay), .out_4(reg_17_out_4));
  Reg reg_18 (.WR(demultiplexer_1_out12), .RegIN(RegIN), .DataINRelay(DataINRelay), .out_4(reg_18_out_4));
  Reg reg_19 (.WR(demultiplexer_1_out20), .RegIN(RegIN), .DataINRelay(DataINRelay), .out_4(reg_19_out_4));
  Reg reg_20 (.WR(demultiplexer_1_out28), .RegIN(RegIN), .DataINRelay(DataINRelay), .out_4(reg_20_out_4));
  Reg reg_21 (.WR(demultiplexer_1_out5), .RegIN(RegIN), .DataINRelay(DataINRelay), .out_4(reg_21_out_4));
  Reg reg_22 (.WR(demultiplexer_1_out13), .RegIN(RegIN), .DataINRelay(DataINRelay), .out_4(reg_22_out_4));
  Reg reg_23 (.WR(demultiplexer_1_out21), .RegIN(RegIN), .DataINRelay(DataINRelay), .out_4(reg_23_out_4));
  Reg reg_24 (.WR(demultiplexer_1_out29), .RegIN(RegIN), .DataINRelay(DataINRelay), .out_4(reg_24_out_4));
  Reg reg_25 (.WR(demultiplexer_1_out6), .RegIN(RegIN), .DataINRelay(DataINRelay), .out_4(reg_25_out_4));
  Reg reg_26 (.WR(demultiplexer_1_out14), .RegIN(RegIN), .DataINRelay(DataINRelay), .out_4(reg_26_out_4));
  Reg reg_27 (.WR(demultiplexer_1_out22), .RegIN(RegIN), .DataINRelay(DataINRelay), .out_4(reg_27_out_4));
  Reg reg_28 (.WR(demultiplexer_1_out30), .RegIN(RegIN), .DataINRelay(DataINRelay), .out_4(reg_28_out_4));
  Reg reg_29 (.WR(demultiplexer_1_out7), .RegIN(RegIN), .DataINRelay(DataINRelay), .out_4(reg_29_out_4));
  Reg reg_30 (.WR(demultiplexer_1_out15), .RegIN(RegIN), .DataINRelay(DataINRelay), .out_4(reg_30_out_4));
  Reg reg_31 (.WR(demultiplexer_1_out23), .RegIN(RegIN), .DataINRelay(DataINRelay), .out_4(reg_31_out_4));
  Reg reg_32 (.WR(demultiplexer_1_out31), .RegIN(RegIN), .DataINRelay(DataINRelay), .out_4(reg_32_out_4));
  Multiplexer #(.select(5), .width(32)) multiplexer_1 (
    .in0(reg_1_out_4), .in1(reg_5_out_4), .in2(reg_9_out_4), .in3(reg_13_out_4), .in4(reg_17_out_4),
    .in5(reg_21_out_4), .in6(reg_25_out_4), .in7(reg_29_out_4), .in8(reg_2_out_4), .in9(reg_6_out_4),
    .in10(reg_10_out_4), .in11(reg_14_out_4), .in12(reg_18_out_4), .in13(reg_22_out_4), .in14(reg_26_out_4),
    .in15(reg_30_out_4), .in16(reg_3_out_4), .in17(reg_7_out_4), .in18(reg_11_out_4), .in19(reg_15_out_4),
    .in20(reg_19_out_4), .in21(reg_23_out_4), .in22(reg_27_out_4), .in23(reg_31_out_4), .in24(reg_4_out_4),
    .in25(reg_8_out_4), .in26(reg_12_out_4), .in27(reg_16_out_4), .in28(reg_20_out_4), .in29(reg_24_out_4),
    .in30(reg_28_out_4), .in31(reg_32_out_4), .out(DATAReg_A), .sel(RegDATA_A));  // open: en
endmodule

module Unidade_de_controle (
  input  [31:0] \Instrução ,
  output [15:0] Dado_externo,
  output Gera_E,
  output [4:0] OpCode,
  output [4:0] RegA,
  output [4:0] RegB,
  output [4:0] RegW,
  output [4:0] SA
);

  and and_1 (Gera_E, ~\Instrução [31], ~\Instrução [30], \Instrução [29], \Instrução [28], \Instrução [27]);  // AND_Gate

  assign Dado_externo = {\Instrução [20:17], \Instrução [11:0]};
  assign OpCode = \Instrução [31:27];
  assign RegA = \Instrução [26:22];
  assign RegB = \Instrução [21:17];
  assign RegW = \Instrução [16:12];
  assign SA = \Instrução [11:7];
endmodule
