// Logisim project Registrador.circ as structural Verilog
module Registrador (
  input  [31:0] DataIN,
  input  WR,
  output [31:0] RegDATA,
  output [31:0] RegDATA_2
);

  D_Flip_Flop _31 (.clk(WR), .D(DataIN[31]), .Q(RegDATA_2[31]));  // open: Qn, preset, en, reset
  D_Flip_Flop _23 (.clk(WR), .D(DataIN[23]), .Q(RegDATA_2[23]));  // open: Qn, preset, en, reset
  D_Flip_Flop _15 (.clk(WR), .D(DataIN[15]), .Q(RegDATA_2[15]));  // open: Qn, preset, en, reset
  D_Flip_Flop _7 (.clk(WR), .D(DataIN[7]), .Q(RegDATA_2[7]));  // open: Qn, preset, en, reset
  D_Flip_Flop _30 (.clk(WR), .D(DataIN[30]), .Q(RegDATA_2[30]));  // open: Qn, preset, en, reset
  D_Flip_Flop _22 (.clk(WR), .D(DataIN[22]), .Q(RegDATA_2[22]));  // open: Qn, preset, en, reset
  D_Flip_Flop _14 (.clk(WR), .D(DataIN[14]), .Q(RegDATA_2[14]));  // open: Qn, preset, en, reset
  D_Flip_Flop _6 (.clk(WR), .D(DataIN[6]), .Q(RegDATA_2[6]));  // open: Qn, preset, en, reset
  D_Flip_Flop _29 (.clk(WR), .D(DataIN[29]), .Q(RegDATA_2[29]));  // open: Qn, preset, en, reset
  D_Flip_Flop _21 (.clk(WR), .D(DataIN[21]), .Q(RegDATA_2[21]));  // open: Qn, preset, en, reset
  D_Flip_Flop _13 (.clk(WR), .D(DataIN[13]), .Q(RegDATA_2[13]));  // open: Qn, preset, en, reset
  D_Flip_Flop _5 (.clk(WR), .D(DataIN[5]), .Q(RegDATA_2[5]));  // open: Qn, preset, en, reset
  D_Flip_Flop _28 (.clk(WR), .D(DataIN[28]), .Q(RegDATA_2[28]));  // open: Qn, preset, en, reset
  D_Flip_Flop _20 (.clk(WR), .D(DataIN[20]), .Q(RegDATA_2[20]));  // open: Qn, preset, en, reset
  D_Flip_Flop _12 (.clk(WR), .D(DataIN[12]), .Q(RegDATA_2[12]));  // open: Qn, preset, en, reset
  D_Flip_Flop _4 (.clk(WR), .D(DataIN[4]), .Q(RegDATA_2[4]));  // open: Qn, preset, en, reset
  D_Flip_Flop _27 (.clk(WR), .D(DataIN[27]), .Q(RegDATA_2[27]));  // open: Qn, preset, en, reset
  D_Flip_Flop _19 (.clk(WR), .D(DataIN[19]), .Q(RegDATA_2[19]));  // open: Qn, preset, en, reset
  D_Flip_Flop _11 (.clk(WR), .D(DataIN[11]), .Q(RegDATA_2[11]));  // open: Qn, preset, en, reset
  D_Flip_Flop _3 (.clk(WR), .D(DataIN[3]), .Q(RegDATA_2[3]));  // open: Qn, preset, en, reset
  D_Flip_Flop _26 (.clk(WR), .D(DataIN[26]), .Q(RegDATA_2[26]));  // open: Qn, preset, en, reset
  D_Flip_Flop _18 (.clk(WR), .D(DataIN[18]), .Q(RegDATA_2[18]));  // open: Qn, preset, en, reset
  D_Flip_Flop _10 (.clk(WR), .D(DataIN[10]), .Q(RegDATA_2[10]));  // open: Qn, preset, en, reset
  D_Flip_Flop _2 (.clk(WR), .D(DataIN[2]), .Q(RegDATA_2[2]));  // open: Qn, preset, en, reset
  D_Flip_Flop _25 (.clk(WR), .D(DataIN[25]), .Q(RegDATA_2[25]));  // open: Qn, preset, en, reset
  D_Flip_Flop _17 (.clk(WR), .D(DataIN[17]), .Q(RegDATA_2[17]));  // open: Qn, preset, en, reset
  D_Flip_Flop _9 (.clk(WR), .D(DataIN[9]), .Q(RegDATA_2[9]));  // open: Qn, preset, en, reset
  D_Flip_Flop _1 (.clk(WR), .D(DataIN[1]), .Q(RegDATA_2[1]));  // open: Qn, preset, en, reset
  D_Flip_Flop _24 (.clk(WR), .D(DataIN[24]), .Q(RegDATA_2[24]));  // open: Qn, preset, en, reset
  D_Flip_Flop _16 (.clk(WR), .D(DataIN[16]), .Q(RegDATA_2[16]));  // open: Qn, preset, en, reset
  D_Flip_Flop _8 (.clk(WR), .D(DataIN[8]), .Q(RegDATA_2[8]));  // open: Qn, preset, en, reset
  D_Flip_Flop _0 (.clk(WR), .D(DataIN[0]), .Q(RegDATA_2[0]));  // open: Qn, preset, en, reset

  assign RegDATA = DataIN;
endmodule

module Reg (
  input  WR,
  input  [4:0] RegWR,
  input  [31:0] RegIN,
  input  [4:0] DataREG,
  output [31:0] DataINRelay,
  output [31:0] RegDATA
);

  wire demultiplexer_1_out0, demultiplexer_1_out1, demultiplexer_1_out2, demultiplexer_1_out3,
       demultiplexer_1_out4, demultiplexer_1_out5, demultiplexer_1_out6, demultiplexer_1_out7,
       demultiplexer_1_out8, demultiplexer_1_out9, demultiplexer_1_out10, demultiplexer_1_out11,
       demultiplexer_1_out12, demultiplexer_1_out13, demultiplexer_1_out14, demultiplexer_1_out15,
       demultiplexer_1_out16, demultiplexer_1_out17, demultiplexer_1_out18, demultiplexer_1_out19,
       demultiplexer_1_out20, demultiplexer_1_out21, demultiplexer_1_out22, demultiplexer_1_out23,
       demultiplexer_1_out24, demultiplexer_1_out25, demultiplexer_1_out26, demultiplexer_1_out27,
       demultiplexer_1_out28, demultiplexer_1_out29, demultiplexer_1_out30, demultiplexer_1_out31;
  wire [31:0] registrador_1_regdata_2, registrador_2_regdata_2, registrador_3_regdata_2,
       registrador_4_regdata_2, registrador_5_regdata_2, registrador_6_regdata_2, registrador_7_regdata_2,
       registrador_8_regdata_2, registrador_9_regdata_2, registrador_10_regdata_2, registrador_11_regdata_2,
       registrador_12_regdata_2, registrador_13_regdata_2, registrador_14_regdata_2,
       registrador_15_regdata_2, registrador_16_regdata_2, registrador_17_regdata_2,
       registrador_18_regdata_2, registrador_19_regdata_2, registrador_20_regdata_2,
       registrador_21_regdata_2, registrador_22_regdata_2, registrador_23_regdata_2,
       registrador_24_regdata_2, registrador_25_regdata_2, registrador_26_regdata_2,
       registrador_27_regdata_2, registrador_28_regdata_2, registrador_29_regdata_2,
       registrador_30_regdata_2, registrador_31_regdata_2, registrador_32_regdata_2;

  Demultiplexer #(.select(5)) demultiplexer_1 (
    .out0(demultiplexer_1_out0), .out1(demultiplexer_1_out1), .out2(demultiplexer_1_out2),
    .out3(demultiplexer_1_out3), .out4(demultiplexer_1_out4), .out5(demultiplexer_1_out5),
    .out6(demultiplexer_1_out6), .out7(demultiplexer_1_out7), .out8(demultiplexer_1_out8),
    .out9(demultiplexer_1_out9), .out10(demultiplexer_1_out10), .out11(demultiplexer_1_out11),
    .out12(demultiplexer_1_out12), .out13(demultiplexer_1_out13), .out14(demultiplexer_1_out14),
    .out15(demultiplexer_1_out15), .out16(demultiplexer_1_out16), .out17(demultiplexer_1_out17),
    .out18(demultiplexer_1_out18), .out19(demultiplexer_1_out19), .out20(demultiplexer_1_out20),
    .out21(demultiplexer_1_out21), .out22(demultiplexer_1_out22), .out23(demultiplexer_1_out23),
    .out24(demultiplexer_1_out24), .out25(demultiplexer_1_out25), .out26(demultiplexer_1_out26),
    .out27(demultiplexer_1_out27), .out28(demultiplexer_1_out28), .out29(demultiplexer_1_out29),
    .out30(demultiplexer_1_out30), .out31(demultiplexer_1_out31), .in(WR), .sel(RegWR));  // open: en
  Registrador registrador_1 (
    .WR(demultiplexer_1_out0), .RegDATA_2(registrador_1_regdata_2), .DataIN(RegIN), .RegDATA(DataINRelay));
  Registrador registrador_2 (
    .WR(demultiplexer_1_out8), .RegDATA_2(registrador_2_regdata_2), .DataIN(RegIN), .RegDATA(DataINRelay));
  Registrador registrador_3 (
    .WR(demultiplexer_1_out16), .RegDATA_2(registrador_3_regdata_2), .DataIN(RegIN), .RegDATA(DataINRelay));
  Registrador registrador_4 (
    .WR(demultiplexer_1_out24), .RegDATA_2(registrador_4_regdata_2), .DataIN(RegIN), .RegDATA(DataINRelay));
  Registrador registrador_5 (
    .WR(demultiplexer_1_out1), .RegDATA_2(registrador_5_regdata_2), .DataIN(RegIN), .RegDATA(DataINRelay));
  Registrador registrador_6 (
    .WR(demultiplexer_1_out9), .RegDATA_2(registrador_6_regdata_2), .DataIN(RegIN), .RegDATA(DataINRelay));
  Registrador registrador_7 (
    .WR(demultiplexer_1_out17), .RegDATA_2(registrador_7_regdata_2), .DataIN(RegIN), .RegDATA(DataINRelay));
  Registrador registrador_8 (
    .WR(demultiplexer_1_out25), .RegDATA_2(registrador_8_regdata_2), .DataIN(RegIN), .RegDATA(DataINRelay));
  Registrador registrador_9 (
    .WR(demultiplexer_1_out2), .RegDATA_2(registrador_9_regdata_2), .DataIN(RegIN), .RegDATA(DataINRelay));
  Registrador registrador_10 (
    .WR(demultiplexer_1_out10), .RegDATA_2(registrador_10_regdata_2), .DataIN(RegIN), .RegDATA(DataINRelay));
  Registrador registrador_11 (
    .WR(demultiplexer_1_out18), .RegDATA_2(registrador_11_regdata_2), .DataIN(RegIN), .RegDATA(DataINRelay));
  Registrador registrador_12 (
    .WR(demultiplexer_1_out26), .RegDATA_2(registrador_12_regdata_2), .DataIN(RegIN), .RegDATA(DataINRelay));
  Registrador registrador_13 (
    .WR(demultiplexer_1_out3), .RegDATA_2(registrador_13_regdata_2), .DataIN(RegIN), .RegDATA(DataINRelay));
  Registrador registrador_14 (
    .WR(demultiplexer_1_out11), .RegDATA_2(registrador_14_regdata_2), .DataIN(RegIN), .RegDATA(DataINRelay));
  Registrador registrador_15 (
    .WR(demultiplexer_1_out19), .RegDATA_2(registrador_15_regdata_2), .DataIN(RegIN), .RegDATA(DataINRelay));
  Registrador registrador_16 (
    .WR(demultiplexer_1_out27), .RegDATA_2(registrador_16_regdata_2), .DataIN(RegIN), .RegDATA(DataINRelay));
  Registrador registrador_17 (
    .WR(demultiplexer_1_out4), .RegDATA_2(registrador_17_regdata_2), .DataIN(RegIN), .RegDATA(DataINRelay));
  Registrador registrador_18 (
    .WR(demultiplexer_1_out12), .RegDATA_2(registrador_18_regdata_2), .DataIN(RegIN), .RegDATA(DataINRelay));
  Registrador registrador_19 (
    .WR(demultiplexer_1_out20), .RegDATA_2(registrador_19_regdata_2), .DataIN(RegIN), .RegDATA(DataINRelay));
  Registrador registrador_20 (
    .WR(demultiplexer_1_out28), .RegDATA_2(registrador_20_regdata_2), .DataIN(RegIN), .RegDATA(DataINRelay));
  Registrador registrador_21 (
    .WR(demultiplexer_1_out5), .RegDATA_2(registrador_21_regdata_2), .DataIN(RegIN), .RegDATA(DataINRelay));
  Registrador registrador_22 (
    .WR(demultiplexer_1_out13), .RegDATA_2(registrador_22_regdata_2), .DataIN(RegIN), .RegDATA(DataINRelay));
  Registrador registrador_23 (
    .WR(demultiplexer_1_out21), .RegDATA_2(registrador_23_regdata_2), .DataIN(RegIN), .RegDATA(DataINRelay));
  Registrador registrador_24 (
    .WR(demultiplexer_1_out29), .RegDATA_2(registrador_24_regdata_2), .DataIN(RegIN), .RegDATA(DataINRelay));
  Registrador registrador_25 (
    .WR(demultiplexer_1_out6), .RegDATA_2(registrador_25_regdata_2), .DataIN(RegIN), .RegDATA(DataINRelay));
  Registrador registrador_26 (
    .WR(demultiplexer_1_out14), .RegDATA_2(registrador_26_regdata_2), .DataIN(RegIN), .RegDATA(DataINRelay));
  Registrador registrador_27 (
    .WR(demultiplexer_1_out22), .RegDATA_2(registrador_27_regdata_2), .DataIN(RegIN), .RegDATA(DataINRelay));
  Registrador registrador_28 (
    .WR(demultiplexer_1_out30), .RegDATA_2(registrador_28_regdata_2), .DataIN(RegIN), .RegDATA(DataINRelay));
  Registrador registrador_29 (
    .WR(demultiplexer_1_out7), .RegDATA_2(registrador_29_regdata_2), .DataIN(RegIN), .RegDATA(DataINRelay));
  Registrador registrador_30 (
    .WR(demultiplexer_1_out15), .RegDATA_2(registrador_30_regdata_2), .DataIN(RegIN), .RegDATA(DataINRelay));
  Registrador registrador_31 (
    .WR(demultiplexer_1_out23), .RegDATA_2(registrador_31_regdata_2), .DataIN(RegIN), .RegDATA(DataINRelay));
  Registrador registrador_32 (
    .WR(demultiplexer_1_out31), .RegDATA_2(registrador_32_regdata_2), .DataIN(RegIN), .RegDATA(DataINRelay));
  Multiplexer #(.select(5), .width(32)) multiplexer_1 (
    .in0(registrador_1_regdata_2), .in1(registrador_5_regdata_2), .in2(registrador_9_regdata_2),
    .in3(registrador_13_regdata_2), .in4(registrador_17_regdata_2), .in5(registrador_21_regdata_2),
    .in6(registrador_25_regdata_2), .in7(registrador_29_regdata_2), .in8(registrador_2_regdata_2),
    .in9(registrador_6_regdata_2), .in10(registrador_10_regdata_2), .in11(registrador_14_regdata_2),
    .in12(registrador_18_regdata_2), .in13(registrador_22_regdata_2), .in14(registrador_26_regdata_2),
    .in15(registrador_30_regdata_2), .in16(registrador_3_regdata_2), .in17(registrador_7_regdata_2),
    .in18(registrador_11_regdata_2), .in19(registrador_15_regdata_2), .in20(registrador_19_regdata_2),
    .in21(registrador_23_regdata_2), .in22(registrador_27_regdata_2), .in23(registrador_31_regdata_2),
    .in24(registrador_4_regdata_2), .in25(registrador_8_regdata_2), .in26(registrador_12_regdata_2),
    .in27(registrador_16_regdata_2), .in28(registrador_20_regdata_2), .in29(registrador_24_regdata_2),
    .in30(registrador_28_regdata_2), .in31(registrador_32_regdata_2), .out(RegDATA), .sel(DataREG));  // open: en
endmodule
