// Logisim project ULA_SE4bB1Y.circ as structural Verilog: 8 circuits, main circuit main
module main (
  input  [3:0] in_1,
  input  [3:0] in_2,
  input  [2:0] in_3,
  input  [1:0] in_4,
  output out_5,
  output [3:0] out_6,
  output out_7
);

  ULA4 ula4_1 (.A(in_1), .B(in_2), .OpCode(in_3), .SA(in_4), .zero(out_5), .ULAS(out_6), .OverflowN(out_7));
endmodule

module mux4 (
  input  A,
  input  B,
  input  C,
  input  D,
  input  Sel1,
  input  Sel0,
  output S
);

  wire and_1_out, and_2_out, and_3_out, and_4_out;

  and and_1 (and_1_out, A, ~Sel0, ~Sel1);  // AND_Gate
  and and_2 (and_2_out, B, Sel0, ~Sel1);  // AND_Gate
  and and_3 (and_3_out, C, ~Sel0, Sel1);  // AND_Gate
  and and_4 (and_4_out, D, Sel0, Sel1);
  or or_1 (S, and_1_out, and_2_out, and_3_out, and_4_out);
endmodule

module mux8 (
  input  A,
  input  B,
  input  C,
  input  D,
  input  E,
  input  F,
  input  G,
  input  H,
  input  Sel2,
  input  Sel1,
  input  Sel0,
  output out_12,
  output out_13,
  output out_14,
  output S
);

  wire mux4_1_s, mux4_2_s;

  mux4 mux4_1 (.A(A), .B(B), .C(C), .D(D), .Sel1(Sel1), .Sel0(Sel0), .S(mux4_1_s));
  mux4 mux4_2 (.A(E), .B(F), .C(G), .D(H), .Sel1(Sel1), .Sel0(Sel0), .S(mux4_2_s));
  mux4 mux4_3 (.A(mux4_1_s), .D(mux4_2_s), .Sel1(Sel2), .Sel0(Sel2), .S(S));  // open: B, C

  assign out_12 = Sel2;
  assign out_13 = Sel1;
  assign out_14 = Sel0;
endmodule

module CelulaULA (
  input  a,
  input  b,
  input  Vem1,
  input  Sel2,
  input  in_5,
  input  Sel0,
  output out_7,
  output out_8,
  output out_9,
  output S,
  output Vai1
);

  wire adder_1_out, and_1_out, nand_1_out, or_1_out, xor_1_out;

  Adder #(.width(1)) adder_1 (.a(a), .b(b), .out(adder_1_out), .cin(Vem1), .cout(Vai1));
  and and_1 (and_1_out, a, b);
  or or_1 (or_1_out, a, b);
  xor xor_1 (xor_1_out, a, b);
  nand nand_1 (nand_1_out, a, b);
  mux8 mux8_1 (
    .A(and_1_out), .B(or_1_out), .C(xor_1_out), .D(adder_1_out), .E(nand_1_out), .F(a), .G(a), .H(1'b0),
    .out_12(out_7), .out_13(out_8), .out_14(out_9), .Sel2(Sel2), .Sel1(in_5), .Sel0(Sel0), .S(S));

  // Notes on the sheet:
  //   000=AND
  //   001=OR
  //   010=XOR
  //   011=SOMA NAT
  //   100=NAND
  //   101=SLL
  //   110=SRL
endmodule

module ULA4 (
  input  [3:0] A,
  input  [1:0] SA,
  input  [3:0] B,
  input  [2:0] OpCode,
  output zero,
  output [3:0] ULAS,
  output OverflowN
);

  wire and_1_out, celulaula_1_vai1, celulaula_2_out_7, celulaula_2_out_8, celulaula_2_out_9,
       celulaula_2_vai1, celulaula_3_out_7, celulaula_3_out_8, celulaula_3_out_9, celulaula_3_vai1,
       celulaula_4_out_7, celulaula_4_out_8, celulaula_4_out_9;
  wire [3:0] shifter_1_a_prime;

  shifter shifter_1 (.A(A), .SA(SA), .L_R(and_1_out), .A_prime(shifter_1_a_prime));
  and and_1 (and_1_out, OpCode[2], ~OpCode[1], OpCode[0]);  // AND_Gate
  CelulaULA celulaula_1 (
    .a(shifter_1_a_prime[0]), .b(B[0]), .Vem1(1'b0), .Sel2(celulaula_2_out_7), .in_5(celulaula_2_out_8),
    .Sel0(celulaula_2_out_9), .S(ULAS[0]), .Vai1(celulaula_1_vai1));  // open: out_7, out_8, out_9
  CelulaULA celulaula_2 (
    .a(shifter_1_a_prime[1]), .b(B[1]), .Vem1(celulaula_1_vai1), .out_7(celulaula_2_out_7),
    .out_8(celulaula_2_out_8), .out_9(celulaula_2_out_9), .Sel2(celulaula_3_out_7), .in_5(celulaula_3_out_8),
    .Sel0(celulaula_3_out_9), .S(ULAS[1]), .Vai1(celulaula_2_vai1));
  CelulaULA celulaula_3 (
    .a(shifter_1_a_prime[2]), .b(B[2]), .Vem1(celulaula_2_vai1), .out_7(celulaula_3_out_7),
    .out_8(celulaula_3_out_8), .out_9(celulaula_3_out_9), .Sel2(celulaula_4_out_7), .in_5(celulaula_4_out_8),
    .Sel0(celulaula_4_out_9), .S(ULAS[2]), .Vai1(celulaula_3_vai1));
  CelulaULA celulaula_4 (
    .a(shifter_1_a_prime[3]), .b(B[3]), .Vem1(celulaula_3_vai1), .out_7(celulaula_4_out_7),
    .out_8(celulaula_4_out_8), .out_9(celulaula_4_out_9), .Sel2(OpCode[2]), .in_5(OpCode[1]),
    .Sel0(OpCode[0]), .S(ULAS[3]), .Vai1(OverflowN));
  nor nor_1 (zero, ULAS[0], ULAS[1], ULAS[2], ULAS[3]);

  // Notes on the sheet:
  //   000=AND
  //   001=OR
  //   010=XOR
  //   011=SOMA NAT
  //   100=NAND
  //   101=SLL
  //   110=SRL
endmodule

module shifter (
  input  [3:0] A,
  input  L_R,
  input  [1:0] SA,
  output [3:0] A_prime
);

  wire [3:0] mux4_1_s, mux4_5_s;

  mux4 mux4_1 (.A(A[0]), .B(A[1]), .C(A[2]), .D(A[3]), .Sel1(SA[1]), .Sel0(SA[0]), .S(mux4_1_s[0]));
  mux4 mux4_2 (.A(A[1]), .B(A[2]), .C(A[3]), .D(1'b0), .Sel1(SA[1]), .Sel0(SA[0]), .S(mux4_1_s[1]));
  mux4 mux4_3 (.A(A[2]), .B(A[3]), .C(1'b0), .D(1'b0), .Sel1(SA[1]), .Sel0(SA[0]), .S(mux4_1_s[2]));
  mux4 mux4_4 (.A(A[3]), .B(1'b0), .C(1'b0), .D(1'b0), .Sel1(SA[1]), .Sel0(SA[0]), .S(mux4_1_s[3]));
  mux4 mux4_5 (.A(A[0]), .B(1'b0), .C(1'b0), .D(1'b0), .Sel1(SA[1]), .Sel0(SA[0]), .S(mux4_5_s[0]));
  mux4 mux4_6 (.A(A[1]), .B(A[0]), .C(1'b0), .D(1'b0), .Sel1(SA[1]), .Sel0(SA[0]), .S(mux4_5_s[1]));
  mux4 mux4_7 (.A(A[2]), .B(A[1]), .C(A[0]), .D(1'b0), .Sel1(SA[1]), .Sel0(SA[0]), .S(mux4_5_s[2]));
  mux4 mux4_8 (.A(A[3]), .B(A[2]), .C(A[1]), .D(A[0]), .Sel1(SA[1]), .Sel0(SA[0]), .S(mux4_5_s[3]));
  MUX2_4 mux2_4_1 (.in_1(mux4_1_s), .in_2(mux4_5_s), .in_3(L_R), .out_4(A_prime));
endmodule

module MUX2_4 (
  input  [3:0] in_1,
  input  [3:0] in_2,
  input  in_3,
  output [3:0] out_4
);

  MUX2 mux2_1 (.a(in_1[0]), .b(in_2[0]), .Sel(in_3), .S(out_4[0]));
  MUX2 mux2_2 (.a(in_1[1]), .b(in_2[1]), .Sel(in_3), .S(out_4[1]));
  MUX2 mux2_3 (.a(in_1[2]), .b(in_2[2]), .Sel(in_3), .S(out_4[2]));
  MUX2 mux2_4 (.a(in_1[3]), .b(in_2[3]), .Sel(in_3), .S(out_4[3]));
endmodule

module MUX2 (
  input  a,
  input  b,
  input  Sel,
  output S
);

  wire and_1_out, and_2_out;

  and and_1 (and_1_out, a, ~Sel);  // AND_Gate
  and and_2 (and_2_out, b, Sel);
  or or_1 (S, and_1_out, and_2_out);
endmodule
